// Logisim project 16_4encoders.circ as structural Verilog: 1 circuit, main circuit main
module main (
  input  i0,
  input  i1,
  input  i2,
  input  i3,
  input  i4,
  input  i5,
  input  i6,
  input  i7,
  input  i8,
  input  i9,
  input  i10,
  input  i11,
  input  i12,
  input  i13,
  input  i14,
  input  i15
);

  wire a_out, b0_out, b1_out, b2_out, b3_out, b4_out, b5_out, b6_out, b7_out, b8_out, b9_out, b10_out,
       b11_out, b12_out, b13_out, b14_out, b15_out, b_out, c_out, d_out, e_out, f_out, g_out, not_1_out,
       not_2_out, not_3_out, not_4_out, o0_out, o1_out, o2_out, o3_out;

  or o2 (o2_out, i4, i5, i6, i7, i12, i13, i14, i15);
  or o3 (o3_out, i8, i9, i10, i11, i12, i13, i14, i15);
  or o1 (o1_out, i2, i3, i6, i7, i10, i11, i14, i15);
  or o0 (o0_out, i1, i3, i5, i7, i9, i11, i13, i15);
  not not_1 (not_1_out, o0_out);
  not not_2 (not_2_out, o1_out);
  not not_3 (not_3_out, o2_out);
  not not_4 (not_4_out, o3_out);
  and b0 (b0_out, not_1_out, not_2_out, not_3_out, not_4_out);
  and b1 (b1_out, o0_out, not_2_out, not_3_out, not_4_out);
  and b2 (b2_out, not_1_out, o1_out, not_3_out, not_4_out);
  and b3 (b3_out, o0_out, o1_out, not_3_out, not_4_out);
  and b4 (b4_out, not_1_out, not_2_out, o2_out, not_4_out);
  and b5 (b5_out, o0_out, not_2_out, o2_out, not_4_out);
  and b6 (b6_out, not_1_out, o1_out, o2_out, not_4_out);
  and b7 (b7_out, o0_out, o1_out, o2_out, not_4_out);
  and b8 (b8_out, not_1_out, not_2_out, not_3_out, o3_out);
  and b9 (b9_out, o0_out, not_2_out, not_3_out, o3_out);
  and b10 (b10_out, not_1_out, o1_out, not_3_out, o3_out);
  and b11 (b11_out, o0_out, o1_out, not_3_out, o3_out);
  and b12 (b12_out, not_1_out, not_2_out, o2_out, o3_out);
  and b13 (b13_out, o0_out, not_2_out, o2_out, o3_out);
  and b14 (b14_out, not_1_out, o1_out, o2_out, o3_out);
  and b15 (b15_out, o0_out, o1_out, o2_out, o3_out);
  or a (a_out, b0_out, b2_out, b3_out, b5_out, b6_out, b7_out, b8_out, b9_out, b10_out, b12_out, b14_out, b15_out);
  or b (b_out, b0_out, b1_out, b2_out, b3_out, b4_out, b7_out, b8_out, b9_out, b10_out, b13_out);
  or c (c_out, b0_out, b1_out, b3_out, b4_out, b5_out, b6_out, b7_out, b8_out, b9_out, b10_out, b11_out, b13_out);
  or d (d_out, b0_out, b2_out, b3_out, b5_out, b6_out, b8_out, b9_out, b11_out, b12_out, b13_out, b14_out);
  or e (e_out, b10_out, b0_out, b2_out, b6_out, b8_out, b11_out, b12_out, b14_out, b15_out, b13_out);
  or f (f_out, b0_out, b4_out, b5_out, b6_out, b8_out, b9_out, b10_out, b11_out, b12_out, b14_out, b15_out);
  or g (g_out, b2_out, b3_out, b4_out, b5_out, b6_out, b8_out, b9_out, b10_out, b11_out, b13_out, b14_out, b15_out);
  _7_Segment_Display u_7_segment_display_1 (
    .g(g_out), .f(f_out), .a(a_out), .b(b_out), .e(e_out), .d(d_out), .c(c_out));  // open: dp
endmodule
