// Logisim project 16_4priencoders.circ as structural Verilog: 3 circuits, main circuit true
module main (
  input  I0,
  input  I1,
  input  I2,
  input  I3,
  input  I4,
  input  I5,
  input  I6,
  input  I7,
  input  I8,
  input  I9,
  input  I10,
  input  I11,
  input  I12,
  input  I13,
  input  I14,
  input  I15,
  output a,
  output b,
  output c,
  output d,
  output e,
  output f,
  output g
);

  wire and_1_out, and_2_out, and_3_out, and_4_out, and_5_out, and_6_out, and_7_out, and_8_out, b0_out,
       b1_out, b2_out, b3_out, b4_out, b5_out, b6_out, b7_out, b8_out, b9_out, b10_out, b11_out, b12_out,
       b13_out, b14_out, b15_out, fourtwopriencoders_1_output0, fourtwopriencoders_1_output1,
       fourtwopriencoders_2_output0, fourtwopriencoders_2_output1, fourtwopriencoders_3_output0,
       fourtwopriencoders_3_output1, fourtwopriencoders_4_output0, fourtwopriencoders_4_output1,
       fourtwopriencoders_5_output0, fourtwopriencoders_5_output1, judge0_out, judge1_out, judge2_out,
       judge3_out, not_1_out, not_2_out, not_3_out, not_4_out, not_5_out, not_6_out, not_7_out, or_1_out,
       or_2_out;

  fourtwopriencoders fourtwopriencoders_1 (
    .INPUT0(I0), .INPUT1(I1), .INPUT2(I2), .INPUT3(I3), .OUTPUT0(fourtwopriencoders_1_output0),
    .OUTPUT1(fourtwopriencoders_1_output1));
  fourtwopriencoders fourtwopriencoders_2 (
    .INPUT0(I4), .INPUT1(I5), .INPUT2(I6), .INPUT3(I7), .OUTPUT0(fourtwopriencoders_2_output0),
    .OUTPUT1(fourtwopriencoders_2_output1));
  fourtwopriencoders fourtwopriencoders_3 (
    .INPUT0(I8), .INPUT1(I9), .INPUT2(I10), .INPUT3(I11), .OUTPUT0(fourtwopriencoders_3_output0),
    .OUTPUT1(fourtwopriencoders_3_output1));
  fourtwopriencoders fourtwopriencoders_4 (
    .INPUT0(I12), .INPUT1(I13), .INPUT2(I14), .INPUT3(I15), .OUTPUT0(fourtwopriencoders_4_output0),
    .OUTPUT1(fourtwopriencoders_4_output1));
  not not_1 (not_1_out, judge1_out);
  not not_2 (not_2_out, judge2_out);
  and and_1 (and_1_out, fourtwopriencoders_1_output0, judge0_out, not_1_out, not_2_out, not_3_out);
  and and_2 (and_2_out, fourtwopriencoders_2_output0, judge1_out, not_2_out, not_3_out);
  and and_3 (and_3_out, fourtwopriencoders_3_output0, judge2_out, not_3_out);
  and and_4 (and_4_out, fourtwopriencoders_4_output0, judge3_out);
  not not_3 (not_3_out, judge3_out);
  or judge0 (judge0_out, I3, I2, I1, I0);
  or judge1 (judge1_out, I5, I4, I6, I7);
  or judge2 (judge2_out, I11, I10, I9, I8);
  or judge3 (judge3_out, I15, I14, I13, I12);
  and and_5 (and_5_out, fourtwopriencoders_4_output1, judge3_out);
  and and_6 (and_6_out, fourtwopriencoders_3_output1, judge2_out, not_3_out);
  and and_7 (and_7_out, fourtwopriencoders_2_output1, judge1_out, not_2_out, not_3_out);
  and and_8 (and_8_out, fourtwopriencoders_1_output1, judge0_out, not_1_out, not_2_out, not_3_out);
  or or_1 (or_1_out, and_1_out, and_2_out, and_3_out, and_4_out);
  or or_2 (or_2_out, and_5_out, and_6_out, and_7_out, and_8_out);
  fourtwopriencoders fourtwopriencoders_5 (
    .INPUT0(judge0_out), .INPUT1(judge1_out), .INPUT2(judge2_out), .INPUT3(judge3_out),
    .OUTPUT0(fourtwopriencoders_5_output0), .OUTPUT1(fourtwopriencoders_5_output1));
  not not_4 (not_4_out, or_1_out);
  not not_5 (not_5_out, or_2_out);
  not not_6 (not_6_out, fourtwopriencoders_5_output0);
  not not_7 (not_7_out, fourtwopriencoders_5_output1);
  and b0 (b0_out, not_4_out, not_5_out, not_6_out, not_7_out);
  and b1 (b1_out, or_1_out, not_5_out, not_6_out, not_7_out);
  and b2 (b2_out, not_4_out, or_2_out, not_6_out, not_7_out);
  and b3 (b3_out, or_1_out, or_2_out, not_6_out, not_7_out);
  and b4 (b4_out, not_4_out, not_5_out, fourtwopriencoders_5_output0, not_7_out);
  and b5 (b5_out, or_1_out, not_5_out, fourtwopriencoders_5_output0, not_7_out);
  and b6 (b6_out, not_4_out, or_2_out, fourtwopriencoders_5_output0, not_7_out);
  and b7 (b7_out, or_1_out, or_2_out, fourtwopriencoders_5_output0, not_7_out);
  and b8 (b8_out, not_4_out, not_5_out, not_6_out, fourtwopriencoders_5_output1);
  and b9 (b9_out, or_1_out, not_5_out, not_6_out, fourtwopriencoders_5_output1);
  and b10 (b10_out, not_4_out, or_2_out, not_6_out, fourtwopriencoders_5_output1);
  and b11 (b11_out, or_1_out, or_2_out, not_6_out, fourtwopriencoders_5_output1);
  and b12 (b12_out, not_4_out, not_5_out, fourtwopriencoders_5_output0, fourtwopriencoders_5_output1);
  and b13 (b13_out, or_1_out, not_5_out, fourtwopriencoders_5_output0, fourtwopriencoders_5_output1);
  and b14 (b14_out, not_4_out, or_2_out, fourtwopriencoders_5_output0, fourtwopriencoders_5_output1);
  and b15 (b15_out, or_1_out, or_2_out, fourtwopriencoders_5_output0, fourtwopriencoders_5_output1);
  or or_3 (a, b0_out, b2_out, b3_out, b5_out, b6_out, b7_out, b8_out, b9_out, b10_out, b12_out, b14_out, b15_out);
  or or_4 (b, b0_out, b1_out, b2_out, b3_out, b4_out, b7_out, b8_out, b9_out, b10_out, b13_out);
  or or_5 (c, b0_out, b1_out, b3_out, b4_out, b5_out, b6_out, b7_out, b8_out, b9_out, b10_out, b11_out, b13_out);
  or or_6 (d, b0_out, b2_out, b3_out, b5_out, b6_out, b8_out, b9_out, b11_out, b12_out, b13_out, b14_out);
  or or_7 (e, b10_out, b0_out, b2_out, b6_out, b8_out, b11_out, b12_out, b14_out, b15_out, b13_out);
  or or_8 (f, b0_out, b4_out, b5_out, b6_out, b8_out, b9_out, b10_out, b11_out, b12_out, b14_out, b15_out);
  or or_9 (g, b2_out, b3_out, b4_out, b5_out, b6_out, b8_out, b9_out, b10_out, b11_out, b13_out, b14_out, b15_out);
endmodule

module fourtwopriencoders (
  input  INPUT0,
  input  INPUT1,
  input  INPUT2,
  input  INPUT3,
  output OUTPUT0,
  output OUTPUT1
);

  wire and_1_out, not_1_out;

  and and_1 (and_1_out, INPUT1, not_1_out);
  not not_1 (not_1_out, INPUT2);
  or or_1 (OUTPUT0, and_1_out, INPUT3);
  or or_2 (OUTPUT1, INPUT2, INPUT3);
endmodule

module true (
  input  a0,
  input  a1,
  input  a2,
  input  a3,
  input  a4,
  input  a5,
  input  a6,
  input  a7,
  input  a8,
  input  a9,
  input  a10,
  input  a11,
  input  a12,
  input  a13,
  input  a14,
  input  a15
);

  wire main_1_a, main_1_b, main_1_c, main_1_d, main_1_e, main_1_f, main_1_g;

  main main_1 (
    .I0(a0), .I1(a1), .I2(a2), .I3(a3), .I4(a4), .I5(a5), .I6(a6), .I7(a7), .I8(a8), .I9(a9), .I10(a10),
    .I11(a11), .I12(a12), .I13(a13), .I14(a14), .I15(a15), .a(main_1_a), .b(main_1_b), .c(main_1_c),
    .d(main_1_d), .e(main_1_e), .f(main_1_f), .g(main_1_g));
  _7_Segment_Display u_7_segment_display_1 (
    .g(main_1_g), .f(main_1_f), .a(main_1_a), .b(main_1_b), .e(main_1_e), .d(main_1_d), .c(main_1_c));  // open: dp
endmodule
