// Logisim project 2s_complement_adder.circ as structural Verilog: 1 circuit, main circuit main
module main (
  input  a0,
  input  a1,
  input  a2,
  input  a3,
  input  b0,
  input  b1,
  input  b2,
  input  b3,
  output c0,
  output c1,
  output c2,
  output c3
);

  wire fulladder_1_cout, fulladder_2_cout, fulladder_3_cout, fulladder_4_cout;

  fulladder fulladder_1 (.A(a0), .B(b0), .Cin(fulladder_4_cout), .result(c0), .Cout(fulladder_1_cout));
  fulladder fulladder_2 (.A(a1), .B(b1), .Cin(fulladder_1_cout), .result(c1), .Cout(fulladder_2_cout));
  fulladder fulladder_3 (.A(a2), .B(b2), .Cin(fulladder_2_cout), .result(c2), .Cout(fulladder_3_cout));
  fulladder fulladder_4 (.A(a3), .B(b3), .Cin(fulladder_3_cout), .result(c3), .Cout(fulladder_4_cout));
endmodule
