// Logisim project 2s_complement_adder_overflow_detection.circ as structural Verilog: 2 circuits, main circuit fourbitadder
module fourbitadder (
  input  P0,
  input  Q0,
  input  Cin,
  input  P1,
  input  Q1,
  input  P2,
  input  Q2,
  input  P3,
  input  Q3
);

  wire a_out, and_1_out, and_2_out, b0_out, b1_out, b2_out, b3_out, b4_out, b5_out, b6_out, b7_out, b8_out,
       b9_out, b10_out, b11_out, b12_out, b13_out, b14_out, b15_out, b_out, c_out, d_out, e_out, f_out,
       full_adder_1_cout, full_adder_1_result, full_adder_2_cout, full_adder_2_result, full_adder_3_cout,
       full_adder_3_result, full_adder_4_cout, full_adder_4_result, g_out, not_1_out, not_2_out, not_3_out,
       not_4_out, not_5_out, not_6_out, not_7_out;

  not not_1 (not_1_out, full_adder_3_cout);
  not not_2 (not_2_out, Q3);
  and and_1 (and_1_out, full_adder_3_cout, not_2_out, not_3_out);
  not not_3 (not_3_out, P3);
  and and_2 (and_2_out, not_1_out, Q3, P3);
  // OR_Gate or_1 has open pins: in0=and_1_out, in1=and_2_out, out=open
  LED led_1 ();  // open: in
  full_adder full_adder_1 (.Input0(P0), .Input1(Q0), .Cin(Cin), .result(full_adder_1_result), .Cout(full_adder_1_cout));
  full_adder full_adder_2 (
    .Input0(P1), .Input1(Q1), .Cin(full_adder_1_cout), .result(full_adder_2_result), .Cout(full_adder_2_cout));
  full_adder full_adder_3 (
    .Input0(P2), .Input1(Q2), .Cin(full_adder_2_cout), .result(full_adder_3_result), .Cout(full_adder_3_cout));
  full_adder full_adder_4 (
    .Input0(P3), .Input1(Q3), .Cin(full_adder_3_cout), .result(full_adder_4_result), .Cout(full_adder_4_cout));
  LED led_2 (.in(full_adder_4_cout));
  not not_4 (not_4_out, full_adder_1_result);
  not not_5 (not_5_out, full_adder_2_result);
  not not_6 (not_6_out, full_adder_3_result);
  not not_7 (not_7_out, full_adder_4_result);
  and b0 (b0_out, not_4_out, not_5_out, not_6_out, not_7_out);
  and b1 (b1_out, full_adder_1_result, not_5_out, not_6_out, not_7_out);
  and b2 (b2_out, not_4_out, full_adder_2_result, not_6_out, not_7_out);
  and b3 (b3_out, full_adder_1_result, full_adder_2_result, not_6_out, not_7_out);
  and b4 (b4_out, not_4_out, not_5_out, full_adder_3_result, not_7_out);
  and b5 (b5_out, full_adder_1_result, not_5_out, full_adder_3_result, not_7_out);
  and b6 (b6_out, not_4_out, full_adder_2_result, full_adder_3_result, not_7_out);
  and b7 (b7_out, full_adder_1_result, full_adder_2_result, full_adder_3_result, not_7_out);
  and b8 (b8_out, not_4_out, not_5_out, not_6_out, full_adder_4_result);
  and b9 (b9_out, full_adder_1_result, not_5_out, not_6_out, full_adder_4_result);
  and b10 (b10_out, not_4_out, full_adder_2_result, not_6_out, full_adder_4_result);
  and b11 (b11_out, full_adder_1_result, full_adder_2_result, not_6_out, full_adder_4_result);
  and b12 (b12_out, not_4_out, not_5_out, full_adder_3_result, full_adder_4_result);
  and b13 (b13_out, full_adder_1_result, not_5_out, full_adder_3_result, full_adder_4_result);
  and b14 (b14_out, not_4_out, full_adder_2_result, full_adder_3_result, full_adder_4_result);
  and b15 (b15_out, full_adder_1_result, full_adder_2_result, full_adder_3_result, full_adder_4_result);
  or a (a_out, b0_out, b2_out, b3_out, b5_out, b6_out, b7_out, b8_out, b9_out, b10_out, b12_out, b14_out, b15_out);
  or b (b_out, b0_out, b1_out, b2_out, b3_out, b4_out, b7_out, b8_out, b9_out, b10_out, b13_out);
  or c (c_out, b0_out, b1_out, b3_out, b4_out, b5_out, b6_out, b7_out, b8_out, b9_out, b10_out, b11_out, b13_out);
  or d (d_out, b0_out, b2_out, b3_out, b5_out, b6_out, b8_out, b9_out, b11_out, b12_out, b13_out, b14_out);
  or e (e_out, b10_out, b0_out, b2_out, b6_out, b8_out, b11_out, b12_out, b14_out, b15_out, b13_out);
  or f (f_out, b0_out, b4_out, b5_out, b6_out, b8_out, b9_out, b10_out, b11_out, b12_out, b14_out, b15_out);
  or g (g_out, b2_out, b3_out, b4_out, b5_out, b6_out, b8_out, b9_out, b10_out, b11_out, b13_out, b14_out, b15_out);
  _7_Segment_Display u_7_segment_display_1 (
    .g(g_out), .f(f_out), .a(a_out), .b(b_out), .e(e_out), .d(d_out), .c(c_out));  // open: dp
endmodule

module full_adder (
  input  Input0,
  input  Input1,
  input  Cin,
  output result,
  output Cout
);

  wire and_1_out, and_2_out, xor_1_out;

  and and_1 (and_1_out, Input0, Input1);
  and and_2 (and_2_out, xor_1_out, Cin);
  xor xor_1 (xor_1_out, Input0, Input1);
  xor xor_2 (result, xor_1_out, Cin);
  or or_1 (Cout, and_1_out, and_2_out);
endmodule
