// Logisim project 3_8decoders.circ as structural Verilog: 2 circuits, main circuit decoders
module decoders (
  input  a0,
  input  a1,
  input  a2,
  output b0,
  output b1,
  output b2,
  output b3,
  output b4,
  output b5,
  output b6,
  output b7
);

  wire not_1_out, twofourdecoders_1_output1, twofourdecoders_1_output2, twofourdecoders_1_output3,
       twofourdecoders_1_output4, twofourdecoders_2_output1, twofourdecoders_2_output2,
       twofourdecoders_2_output3, twofourdecoders_2_output4;

  not not_1 (not_1_out, a2);
  twofourdecoders twofourdecoders_1 (
    .Input1(a1), .Input2(a0), .Output1(twofourdecoders_1_output1), .Output2(twofourdecoders_1_output2),
    .Output3(twofourdecoders_1_output3), .Output4(twofourdecoders_1_output4));
  twofourdecoders twofourdecoders_2 (
    .Input1(a1), .Input2(a0), .Output1(twofourdecoders_2_output1), .Output2(twofourdecoders_2_output2),
    .Output3(twofourdecoders_2_output3), .Output4(twofourdecoders_2_output4));
  and and_1 (b0, twofourdecoders_1_output1, not_1_out);
  and and_2 (b1, twofourdecoders_1_output2, not_1_out);
  and and_3 (b2, twofourdecoders_1_output3, not_1_out);
  and and_4 (b3, twofourdecoders_1_output4, not_1_out);
  and and_5 (b4, twofourdecoders_2_output1, a2);
  and and_6 (b5, twofourdecoders_2_output2, a2);
  and and_7 (b6, twofourdecoders_2_output3, a2);
  and and_8 (b7, twofourdecoders_2_output4, a2);

  // Notes on the sheet:
  //   a2a1a0=b7b6b5b4b3b2b1b0
endmodule

module twofourdecoders (
  input  Input1,
  input  Input2,
  output Output1,
  output Output2,
  output Output3,
  output Output4
);

  wire not_1_out, not_2_out;

  not not_1 (not_1_out, Input1);
  not not_2 (not_2_out, Input2);
  and and_1 (Output1, not_1_out, not_2_out);
  and and_2 (Output2, not_1_out, Input2);
  and and_3 (Output3, Input1, not_2_out);
  and and_4 (Output4, Input1, Input2);
endmodule
