// Logisim project 3bit4to1selector.circ as structural Verilog: 1 circuit, main circuit main
module main (
  input  A0,
  input  A1,
  input  A2,
  input  A3,
  input  in_5,
  input  S0,
  input  in_7,
  input  in_8,
  input  S1,
  input  in_10,
  input  in_11,
  input  in_12,
  input  in_13,
  input  in_14,
  output A,
  output B,
  output C
);

  wire and_1_out, and_2_out, and_3_out, and_4_out, and_5_out, and_6_out, and_7_out, and_8_out, and_9_out,
       and_10_out, and_11_out, and_12_out, not_1_out, not_2_out, O0_out, O1_out, O2_out, O3_out;

  not not_1 (not_1_out, S0);
  not not_2 (not_2_out, S1);
  and O0 (O0_out, not_1_out, not_2_out);
  and O1 (O1_out, S0, not_2_out);
  and O2 (O2_out, not_1_out, S1);
  and O3 (O3_out, S0, S1);
  and and_1 (and_1_out, A0, O0_out);
  and and_2 (and_2_out, A1, O1_out);
  and and_3 (and_3_out, A2, O2_out);
  and and_4 (and_4_out, A3, O3_out);
  and and_5 (and_5_out, in_5, O0_out);
  and and_6 (and_6_out, in_7, O1_out);
  and and_7 (and_7_out, in_8, O2_out);
  and and_8 (and_8_out, in_10, O3_out);
  and and_9 (and_9_out, in_11, O0_out);
  and and_10 (and_10_out, in_12, O1_out);
  and and_11 (and_11_out, in_13, O2_out);
  and and_12 (and_12_out, in_14, O3_out);
  or or_1 (A, and_1_out, and_2_out, and_3_out, and_4_out);
  or or_2 (B, and_5_out, and_6_out, and_7_out, and_8_out);
  or or_3 (C, and_9_out, and_10_out, and_11_out, and_12_out);
endmodule
