// Logisim project 4bit_count.circ as structural Verilog: 1 circuit, main circuit fourbitcount
module fourbitcount (
  input  I0,
  input  I1,
  input  I2,
  input  I3
);

  wire CLK_out, fulladder_1_cout, fulladder_1_result, fulladder_2_cout, fulladder_2_result, fulladder_3_cout,
       fulladder_3_result, fulladder_4_result, sevensegment_1_a, sevensegment_1_b, sevensegment_1_c,
       sevensegment_1_d, sevensegment_1_e, sevensegment_1_f, sevensegment_1_g, storage_1_q0, storage_1_q1,
       storage_1_q2, storage_1_q3;

  Clock CLK (.out(CLK_out));
  storage storage_1 (
    .D0(fulladder_1_result), .D1(fulladder_2_result), .D2(fulladder_3_result), .D3(fulladder_4_result),
    .CLK(CLK_out), .Q0(storage_1_q0), .Q1(storage_1_q1), .Q2(storage_1_q2), .Q3(storage_1_q3));
  fulladder fulladder_1 (.A(storage_1_q0), .B(1'b1), .Cin(1'b0), .result(fulladder_1_result), .Cout(fulladder_1_cout));
  fulladder fulladder_2 (
    .A(storage_1_q1), .B(1'b0), .Cin(fulladder_1_cout), .result(fulladder_2_result), .Cout(fulladder_2_cout));
  fulladder fulladder_3 (
    .A(storage_1_q2), .B(1'b0), .Cin(fulladder_2_cout), .result(fulladder_3_result), .Cout(fulladder_3_cout));
  fulladder fulladder_4 (
    .A(storage_1_q3), .B(1'b0), .Cin(fulladder_3_cout), .result(fulladder_4_result));  // open: Cout
  sevensegment sevensegment_1 (
    .a0(fulladder_1_result), .a1(fulladder_2_result), .a2(fulladder_3_result), .a3(fulladder_4_result),
    .A(sevensegment_1_a), .B(sevensegment_1_b), .C(sevensegment_1_c), .D(sevensegment_1_d),
    .E(sevensegment_1_e), .F(sevensegment_1_f), .G(sevensegment_1_g));
  _7_Segment_Display u_7_segment_display_1 (
    .g(sevensegment_1_g), .f(sevensegment_1_f), .a(sevensegment_1_a), .b(sevensegment_1_b),
    .e(sevensegment_1_e), .d(sevensegment_1_d), .c(sevensegment_1_c));  // open: dp
endmodule
