// Logisim project 4bit_sign_and_magnitude_adder.circ as structural Verilog: 2 circuits, main circuit signmagnitudeadder
module signmagnitudeadder (
  input  a0,
  input  a1,
  input  a2,
  input  b0,
  input  b1,
  input  b2,
  input  a3,
  input  b3
);

  wire and_1_out, and_2_out, and_3_out, and_4_out, and_5_out, and_6_out, and_7_out, and_8_out,
       full_adder_1_cout, full_adder_1_result, full_adder_2_cout, full_adder_2_result, full_adder_3_result,
       leddisplay_1_a, leddisplay_1_b, leddisplay_1_c, leddisplay_1_d, leddisplay_1_e, leddisplay_1_f,
       leddisplay_1_g, leddisplay_1_g2, or_1_out, or_2_out, or_3_out, or_4_out, substrator_1_cout,
       substrator_1_result, substrator_2_cout, substrator_2_result, substrator_3_result,
       threebitcomparator_1_c0, threebitcomparator_1_c1, threebitcomparator_1_c2, threebitcomparator_1_c3,
       threebitcomparator_1_d0, threebitcomparator_1_d1, threebitcomparator_1_d2, xnor_1_out, xor_1_out;

  xor xor_1 (xor_1_out, a3, b3);
  xnor xnor_1 (xnor_1_out, a3, b3);
  full_adder full_adder_1 (
    .Input0(a0), .Input1(b0), .result(full_adder_1_result), .Cout(full_adder_1_cout));  // open: Cin
  threebitcomparator threebitcomparator_1 (
    .a3(a3), .a2(a2), .a1(a1), .a0(a0), .b3(b3), .b2(b2), .b1(b1), .b0(b0), .d2(threebitcomparator_1_d2),
    .d1(threebitcomparator_1_d1), .d0(threebitcomparator_1_d0), .c3(threebitcomparator_1_c3),
    .c2(threebitcomparator_1_c2), .c1(threebitcomparator_1_c1), .c0(threebitcomparator_1_c0));
  and and_1 (and_1_out, full_adder_1_result, xnor_1_out);
  and and_2 (and_2_out, xor_1_out, threebitcomparator_1_c3);
  and and_3 (and_3_out, full_adder_2_result, xnor_1_out);
  substrator substrator_1 (
    .A(threebitcomparator_1_c0), .B(threebitcomparator_1_d0), .result(substrator_1_result),
    .Cout(substrator_1_cout));  // open: Cin
  full_adder full_adder_2 (
    .Input0(a1), .Input1(b1), .Cin(full_adder_1_cout), .result(full_adder_2_result), .Cout(full_adder_2_cout));
  and and_4 (and_4_out, full_adder_3_result, xnor_1_out);
  and and_5 (and_5_out, xor_1_out, substrator_1_result);
  substrator substrator_2 (
    .A(threebitcomparator_1_c1), .B(threebitcomparator_1_d1), .Cin(substrator_1_cout),
    .result(substrator_2_result), .Cout(substrator_2_cout));
  full_adder full_adder_3 (
    .Input0(a2), .Input1(b2), .Cin(full_adder_2_cout), .result(full_adder_3_result));  // open: Cout
  and and_6 (and_6_out, xor_1_out, substrator_2_result);
  and and_7 (and_7_out, a3, b3);
  or or_1 (or_1_out, and_1_out, and_5_out);
  or or_2 (or_2_out, and_3_out, and_6_out);
  or or_3 (or_3_out, and_4_out, and_8_out);
  or or_4 (or_4_out, and_7_out, and_2_out);
  substrator substrator_3 (
    .A(threebitcomparator_1_c2), .B(threebitcomparator_1_d2), .Cin(substrator_2_cout),
    .result(substrator_3_result));  // open: Cout
  and and_8 (and_8_out, xor_1_out, substrator_3_result);
  LEDdisplay leddisplay_1 (
    .a0(or_1_out), .a1(or_2_out), .a2(or_3_out), .a3(or_4_out), .A(leddisplay_1_a), .B(leddisplay_1_b),
    .C(leddisplay_1_c), .D(leddisplay_1_d), .E(leddisplay_1_e), .F(leddisplay_1_f), .G(leddisplay_1_g),
    .G2(leddisplay_1_g2));
  _7_Segment_Display u_7_segment_display_1 (.g(leddisplay_1_g2));  // open: f, a, b, e, d, c, dp
  _7_Segment_Display u_7_segment_display_2 (
    .g(leddisplay_1_g), .f(leddisplay_1_f), .a(leddisplay_1_a), .b(leddisplay_1_b), .e(leddisplay_1_e),
    .d(leddisplay_1_d), .c(leddisplay_1_c));  // open: dp
endmodule

module threebitcomparator (
  input  a3,
  input  a2,
  input  a1,
  input  a0,
  input  b3,
  input  b2,
  input  b1,
  input  b0,
  output d2,
  output d1,
  output d0,
  output c3,
  output c2,
  output c1,
  output c0
);

  wire and_1_out, and_2_out, and_3_out, and_4_out, and_5_out, and_6_out, not_1_out, not_2_out, not_3_out,
       not_4_out, not_5_out, not_6_out, or_1_out, or_2_out, xnor_1_out, xnor_2_out, xnor_3_out;

  Multiplexer multiplexer_1 (.in0(b3), .in1(a3), .out(c3), .sel(or_2_out));
  not not_1 (not_1_out, b2);
  Multiplexer multiplexer_2 (.in0(b2), .in1(a2), .out(c2), .sel(or_2_out));
  and and_1 (and_1_out, a2, not_1_out);
  xnor xnor_1 (xnor_1_out, a2, b2);
  Multiplexer multiplexer_3 (.in0(b2), .in1(a2), .out(d2), .sel(not_2_out));
  not not_2 (not_2_out, or_2_out);
  or or_1 (or_1_out, and_1_out, and_4_out, and_6_out);
  and and_2 (and_2_out, xnor_1_out, xnor_2_out, xnor_3_out);
  Multiplexer multiplexer_4 (.in0(b1), .in1(a1), .out(c1), .sel(or_2_out));
  not not_3 (not_3_out, b1);
  or or_2 (or_2_out, or_1_out, and_2_out);
  and and_3 (and_3_out, a1, not_3_out);
  Multiplexer multiplexer_5 (.in0(b1), .in1(a1), .out(d1), .sel(not_4_out));
  not not_4 (not_4_out, or_2_out);
  xnor xnor_2 (xnor_2_out, a1, b1);
  and and_4 (and_4_out, xnor_1_out, and_3_out);
  Multiplexer multiplexer_6 (.in0(b0), .in1(a0), .out(c0), .sel(or_2_out));
  not not_5 (not_5_out, b0);
  and and_5 (and_5_out, a0, not_5_out);
  xnor xnor_3 (xnor_3_out, a0, b0);
  Multiplexer multiplexer_7 (.in0(b0), .in1(a0), .out(d0), .sel(not_6_out));
  not not_6 (not_6_out, or_2_out);
  and and_6 (and_6_out, xnor_1_out, xnor_2_out, and_5_out);
endmodule
