// Logisim project 4bit_storage.circ as structural Verilog: 1 circuit, main circuit storage
module storage (
  input  D0,
  input  D1,
  input  D2,
  input  D3,
  input  CLK,
  output Q0,
  output Q1,
  output Q2,
  output Q3
);

  DFF dff_1 (.D(D0), .EN(1'b1), .CLK(CLK), .Q(Q0));  // open: CLR, NQ
  DFF dff_2 (.D(D1), .EN(1'b1), .CLK(CLK), .Q(Q1));  // open: CLR, NQ
  DFF dff_3 (.D(D2), .EN(1'b1), .CLK(CLK), .Q(Q2));  // open: CLR, NQ
  DFF dff_4 (.D(D3), .EN(1'b1), .CLK(CLK), .Q(Q3));  // open: CLR, NQ
endmodule
