// Logisim project 4bitsubstrator.circ as structural Verilog: 3 circuits, main circuit fourbitsubstrator
module fourbitsubstrator (
  input  A3,
  input  A1,
  input  A2,
  input  B3,
  input  B1,
  input  B2,
  input  A0,
  input  B0
);

  wire sevensegment_1_a, sevensegment_1_b, sevensegment_1_c, sevensegment_1_d, sevensegment_1_e,
       sevensegment_1_f, sevensegment_1_g, sevensegment_2_a, sevensegment_2_b, sevensegment_2_c,
       sevensegment_2_d, sevensegment_2_e, sevensegment_2_f, sevensegment_2_g, sevensegment_3_a,
       sevensegment_3_b, sevensegment_3_c, sevensegment_3_d, sevensegment_3_e, sevensegment_3_f,
       sevensegment_3_g, substrator_1_cout, substrator_1_result, substrator_2_cout, substrator_2_result,
       substrator_3_cout, substrator_3_result, substrator_4_cout, substrator_4_result;

  substrator substrator_1 (.A(A0), .B(B0), .result(substrator_1_result), .Cout(substrator_1_cout));  // open: Cin
  sevensegment sevensegment_1 (
    .a0(A0), .a1(A1), .a2(A2), .a3(A3), .A(sevensegment_1_a), .B(sevensegment_1_b), .C(sevensegment_1_c),
    .D(sevensegment_1_d), .E(sevensegment_1_e), .F(sevensegment_1_f), .G(sevensegment_1_g));
  sevensegment sevensegment_2 (
    .a0(B0), .a1(B1), .a2(B2), .a3(B3), .A(sevensegment_2_a), .B(sevensegment_2_b), .C(sevensegment_2_c),
    .D(sevensegment_2_d), .E(sevensegment_2_e), .F(sevensegment_2_f), .G(sevensegment_2_g));
  _7_Segment_Display u_7_segment_display_1 (
    .g(sevensegment_1_g), .f(sevensegment_1_f), .a(sevensegment_1_a), .b(sevensegment_1_b),
    .e(sevensegment_1_e), .d(sevensegment_1_d), .c(sevensegment_1_c));  // open: dp
  _7_Segment_Display u_7_segment_display_2 (
    .g(sevensegment_2_g), .f(sevensegment_2_f), .a(sevensegment_2_a), .b(sevensegment_2_b),
    .e(sevensegment_2_e), .d(sevensegment_2_d), .c(sevensegment_2_c));  // open: dp
  substrator substrator_2 (
    .A(A1), .B(B1), .Cin(substrator_1_cout), .result(substrator_2_result), .Cout(substrator_2_cout));
  substrator substrator_3 (
    .A(A2), .B(B2), .Cin(substrator_2_cout), .result(substrator_3_result), .Cout(substrator_3_cout));
  sevensegment sevensegment_3 (
    .a0(substrator_1_result), .a1(substrator_2_result), .a2(substrator_3_result), .a3(substrator_4_result),
    .A(sevensegment_3_a), .B(sevensegment_3_b), .C(sevensegment_3_c), .D(sevensegment_3_d),
    .E(sevensegment_3_e), .F(sevensegment_3_f), .G(sevensegment_3_g));
  substrator substrator_4 (
    .A(A3), .B(B3), .Cin(substrator_3_cout), .result(substrator_4_result), .Cout(substrator_4_cout));
  LED led_1 (.in(substrator_4_cout));
  _7_Segment_Display u_7_segment_display_3 (
    .g(sevensegment_3_g), .f(sevensegment_3_f), .a(sevensegment_3_a), .b(sevensegment_3_b),
    .e(sevensegment_3_e), .d(sevensegment_3_d), .c(sevensegment_3_c));  // open: dp
endmodule

module LEDdisplay (
  input  a0,
  input  a1,
  input  a2,
  input  a3,
  output A,
  output B,
  output C,
  output D,
  output E,
  output F,
  output G,
  output G2
);

  wire b0_out, b1_out, b2_out, b3_out, b4_out, b5_out, b6_out, b7_out, not_1_out, not_2_out, not_3_out;

  not not_1 (not_1_out, a0);
  not not_2 (not_2_out, a1);
  not not_3 (not_3_out, a2);
  and b0 (b0_out, not_1_out, not_2_out, not_3_out);
  and b1 (b1_out, a0, not_2_out, not_3_out);
  and b2 (b2_out, not_1_out, a1, not_3_out);
  and b3 (b3_out, a0, a1, not_3_out);
  and b4 (b4_out, not_1_out, not_2_out, a2);
  and b5 (b5_out, a0, not_2_out, a2);
  and b6 (b6_out, not_1_out, a1, a2);
  and b7 (b7_out, a0, a1, a2);
  or or_1 (A, b0_out, b2_out, b3_out, b5_out, b7_out);
  or or_2 (B, b1_out, b0_out, b2_out, b3_out, b4_out, b7_out);
  or or_3 (C, b0_out, b1_out, b3_out, b4_out, b5_out, b6_out, b7_out);
  or or_4 (D, b0_out, b2_out, b3_out, b5_out, b6_out);
  or or_5 (E, b0_out, b2_out, b6_out);
  or or_6 (F, b0_out, b4_out, b5_out, b6_out);
  or or_7 (G, b2_out, b3_out, b4_out, b5_out, b6_out);

  assign G2 = a3;
endmodule

module substrator (
  input  A,
  input  B,
  input  Cin,
  output result,
  output Cout
);

  wire and_1_out, and_2_out, not_1_out, xor_1_out, xor_2_out;

  xor xor_1 (xor_1_out, A, B);
  and and_1 (and_1_out, B, Cin);
  or or_1 (result, xor_1_out, Cin);
  xor xor_2 (xor_2_out, B, Cin);
  not not_1 (not_1_out, A);
  or or_2 (Cout, and_1_out, and_2_out);
  and and_2 (and_2_out, xor_2_out, not_1_out);
endmodule
