// Logisim project D_Flip_Flop.circ as structural Verilog: 2 circuits, main circuit DFF
module DFF (
  input  D,
  input  CLR,
  input  EN,
  input  CLK,
  output Q,
  output NQ
);

  wire dlatch_1_q, dlatch_2_nq, dlatch_2_q, not_1_out, not_2_out, not_3_out, or_1_out;

  not not_1 (not_1_out, EN);
  or or_1 (or_1_out, D, not_1_out);
  not not_2 (not_2_out, CLK);
  Dlatch dlatch_1 (.D(or_1_out), .WE(not_2_out), .Q(dlatch_1_q));  // open: CLR, NQ
  not not_3 (not_3_out, CLR);
  Dlatch dlatch_2 (.D(dlatch_1_q), .WE(CLK), .Q(dlatch_2_q), .NQ(dlatch_2_nq));  // open: CLR
  and and_1 (Q, not_3_out, dlatch_2_q);
  or or_2 (NQ, dlatch_2_nq, CLR);
endmodule

module DFFTest (
  output out_1,
  output out_2
);

  wire clock_1_out, not_1_out;

  Clock clock_1 (.out(clock_1_out));
  not not_1 (not_1_out, out_1);
  DFF dff_1 (.D(clock_1_out), .CLR(not_1_out), .Q(out_1), .NQ(out_2));  // open: EN, CLK
endmodule
