// Logisim project D_latch.circ as structural Verilog: 2 circuits, main circuit Test
module Dlatch (
  input  CLR,
  input  D,
  input  WE,
  output Q,
  output NQ
);

  wire and_1_out, and_2_out, and_3_out, nor_1_out, not_1_out, not_2_out;

  not not_1 (not_1_out, D);
  and and_1 (and_1_out, D, WE);
  and and_2 (and_2_out, WE, not_1_out);
  and and_3 (and_3_out, and_2_out, not_2_out);
  nor nor_1 (nor_1_out, and_1_out, NQ);
  nor nor_2 (NQ, Q, and_3_out);
  not not_2 (not_2_out, CLR);
  and and_4 (Q, not_2_out, nor_1_out);
endmodule

module Test (
  input  in_1,
  input  in_2,
  input  in_3,
  output out_4,
  output out_5
);

  wire and_1_out, not_1_out;

  and and_1 (and_1_out, in_1, not_1_out);
  not not_1 (not_1_out, out_4);
  Dlatch dlatch_1 (.CLR(in_2), .D(and_1_out), .WE(in_3), .Q(out_4), .NQ(out_5));
endmodule
