// Logisim project NS_NR_latch.circ as structural Verilog: 1 circuit, main circuit main
module main (
  input  NS,
  input  in_2,
  input  NR,
  output out_4,
  output out_5
);

  wire and_1_out, and_2_out;

  and and_1 (and_1_out, NS, in_2);
  and and_2 (and_2_out, in_2, NR);
  nand nand_1 (out_4, and_1_out, out_5);
  nand nand_2 (out_5, out_4, and_2_out);
endmodule
