// Logisim project XNOR.circ as structural Verilog: 1 circuit, main circuit main
module main (
  input  in_1,
  input  in_2,
  output out_3
);

  wire not_1_out, not_2_out;

  not not_1 (not_1_out, in_1);
  not not_2 (not_2_out, in_2);
  // Transmission_Gate transmission_1: pin names not known; wires that end beside it: in_2, not_1_out, in_1, out_3
  // Transmission_Gate transmission_2: pin names not known; wires that end beside it: not_2_out, not_1_out, out_3
endmodule
