// Logisim project XOR.circ as structural Verilog: 1 circuit, main circuit main
module main (
  input  A,
  input  B,
  output out_3
);

  wire not_1_out, not_2_out;

  not not_1 (not_1_out, A);
  not not_2 (not_2_out, B);
  // Transmission_Gate transmission_1: pin names not known; wires that end beside it: not_2_out, not_1_out, A, out_3
  // Transmission_Gate transmission_2: pin names not known; wires that end beside it: B, not_1_out, out_3
endmodule
