// Logisim project electricity_clock.circ as structural Verilog: 4 circuits, main circuit digitalclock
module digitalclock (
  input  Set,
  input  Reset
);

  wire clock_1_out, decade_1_q0, decade_1_q1, decade_1_q2, decade_1_q3, decade_2_cout, decade_2_q0,
       decade_2_q1, decade_2_q2, decade_2_q3, digitaldisplay_1_a, digitaldisplay_1_b, digitaldisplay_1_c,
       digitaldisplay_1_d, digitaldisplay_1_e, digitaldisplay_1_f, digitaldisplay_1_g, digitaldisplay_2_a,
       digitaldisplay_2_b, digitaldisplay_2_c, digitaldisplay_2_d, digitaldisplay_2_e, digitaldisplay_2_f,
       digitaldisplay_2_g, digitaldisplay_3_a, digitaldisplay_3_b, digitaldisplay_3_c, digitaldisplay_3_d,
       digitaldisplay_3_e, digitaldisplay_3_f, digitaldisplay_3_g, digitaldisplay_4_a, digitaldisplay_4_b,
       digitaldisplay_4_c, digitaldisplay_4_d, digitaldisplay_4_e, digitaldisplay_4_f, digitaldisplay_4_g,
       reunit_1_cout, reunit_1_q0, reunit_1_q1, reunit_1_q2, reunit_1_q3, unit_1_cout, unit_1_q0, unit_1_q1,
       unit_1_q2, unit_1_q3;

  Clock clock_1 (.out(clock_1_out));
  decade decade_1 (
    .CLK(clock_1_out), .Set(Set), .Reset(Reset), .Cin(reunit_1_cout), .Q3(decade_1_q3), .Q2(decade_1_q2),
    .Q1(decade_1_q1), .Q0(decade_1_q0));  // open: Cout
  digitaldisplay digitaldisplay_1 (
    .I0(decade_1_q0), .I1(decade_1_q1), .I2(decade_1_q2), .I3(decade_1_q3), .A(digitaldisplay_1_a),
    .B(digitaldisplay_1_b), .C(digitaldisplay_1_c), .D(digitaldisplay_1_d), .E(digitaldisplay_1_e),
    .F(digitaldisplay_1_f), .G(digitaldisplay_1_g));
  _7_Segment_Display u_7_segment_display_1 (
    .g(digitaldisplay_1_g), .f(digitaldisplay_1_f), .a(digitaldisplay_1_a), .b(digitaldisplay_1_b),
    .e(digitaldisplay_1_e), .d(digitaldisplay_1_d), .c(digitaldisplay_1_c));  // open: dp
  reunit reunit_1 (
    .CLK(clock_1_out), .Set(Set), .Reset(Reset), .Cin(decade_2_cout), .Q3(reunit_1_q3), .Q2(reunit_1_q2),
    .Q1(reunit_1_q1), .Q0(reunit_1_q0), .Cout(reunit_1_cout));
  digitaldisplay digitaldisplay_2 (
    .I0(reunit_1_q0), .I1(reunit_1_q1), .I2(reunit_1_q2), .I3(reunit_1_q3), .A(digitaldisplay_2_a),
    .B(digitaldisplay_2_b), .C(digitaldisplay_2_c), .D(digitaldisplay_2_d), .E(digitaldisplay_2_e),
    .F(digitaldisplay_2_f), .G(digitaldisplay_2_g));
  _7_Segment_Display u_7_segment_display_2 (
    .g(digitaldisplay_2_g), .f(digitaldisplay_2_f), .a(digitaldisplay_2_a), .b(digitaldisplay_2_b),
    .e(digitaldisplay_2_e), .d(digitaldisplay_2_d), .c(digitaldisplay_2_c));  // open: dp
  decade decade_2 (
    .CLK(clock_1_out), .Set(Set), .Reset(Reset), .Cin(unit_1_cout), .Q3(decade_2_q3), .Q2(decade_2_q2),
    .Q1(decade_2_q1), .Q0(decade_2_q0), .Cout(decade_2_cout));
  digitaldisplay digitaldisplay_3 (
    .I0(decade_2_q0), .I1(decade_2_q1), .I2(decade_2_q2), .I3(decade_2_q3), .A(digitaldisplay_3_a),
    .B(digitaldisplay_3_b), .C(digitaldisplay_3_c), .D(digitaldisplay_3_d), .E(digitaldisplay_3_e),
    .F(digitaldisplay_3_f), .G(digitaldisplay_3_g));
  _7_Segment_Display u_7_segment_display_3 (
    .g(digitaldisplay_3_g), .f(digitaldisplay_3_f), .a(digitaldisplay_3_a), .b(digitaldisplay_3_b),
    .e(digitaldisplay_3_e), .d(digitaldisplay_3_d), .c(digitaldisplay_3_c));  // open: dp
  unit unit_1 (
    .CLK(clock_1_out), .Set(Set), .Reset(Reset), .Cin(1'b0), .Q3(unit_1_q3), .Q2(unit_1_q2), .Q1(unit_1_q1),
    .Q0(unit_1_q0), .Cout(unit_1_cout));
  digitaldisplay digitaldisplay_4 (
    .I0(unit_1_q0), .I1(unit_1_q1), .I2(unit_1_q2), .I3(unit_1_q3), .A(digitaldisplay_4_a),
    .B(digitaldisplay_4_b), .C(digitaldisplay_4_c), .D(digitaldisplay_4_d), .E(digitaldisplay_4_e),
    .F(digitaldisplay_4_f), .G(digitaldisplay_4_g));
  _7_Segment_Display u_7_segment_display_4 (
    .g(digitaldisplay_4_g), .f(digitaldisplay_4_f), .a(digitaldisplay_4_a), .b(digitaldisplay_4_b),
    .e(digitaldisplay_4_e), .d(digitaldisplay_4_d), .c(digitaldisplay_4_c));  // open: dp

  // Notes on the sheet:
  //   minute
  //   second
endmodule

module unit (
  input  CLK,
  input  Set,
  input  Reset,
  input  Cin,
  output Q3,
  output Q2,
  output Q1,
  output Q0,
  output Cout
);

  wire digitaldisplay_1_a, digitaldisplay_1_b, digitaldisplay_1_c, digitaldisplay_1_d, digitaldisplay_1_e,
       digitaldisplay_1_f, digitaldisplay_1_g, fourbitadder_1_c0, fourbitadder_1_c1, fourbitadder_1_c2,
       fourbitadder_1_c3, multiplexer_1_out, multiplexer_2_out, multiplexer_3_out, multiplexer_4_out,
       not_1_out, not_2_out;

  fourbitDFF fourbitdff_1 (
    .D0(multiplexer_1_out), .D1(multiplexer_2_out), .D2(multiplexer_3_out), .D3(multiplexer_4_out),
    .CLK(CLK), .S(Set), .R(Reset), .Q0(Q0), .Q1(Q1), .Q2(Q2), .Q3(Q3));  // open: NQ0, NQ1, NQ2, NQ3
  fourbitadder fourbitadder_1 (
    .a0(Q0), .a1(Q1), .a2(Q2), .a3(Q3), .b0(1'b1), .b1(1'b0), .b2(1'b0), .b3(1'b0), .Cin(Cin),
    .c0(fourbitadder_1_c0), .c1(fourbitadder_1_c1), .c2(fourbitadder_1_c2), .c3(fourbitadder_1_c3));  // open: Cout
  digitaldisplay digitaldisplay_1 (
    .I0(Q0), .I1(Q1), .I2(Q2), .I3(Q3), .A(digitaldisplay_1_a), .B(digitaldisplay_1_b),
    .C(digitaldisplay_1_c), .D(digitaldisplay_1_d), .E(digitaldisplay_1_e), .F(digitaldisplay_1_f),
    .G(digitaldisplay_1_g));
  not not_1 (not_1_out, fourbitadder_1_c0);
  not not_2 (not_2_out, fourbitadder_1_c2);
  and and_1 (Cout, not_1_out, fourbitadder_1_c1, not_2_out, fourbitadder_1_c3);
  _7_Segment_Display u_7_segment_display_1 (
    .g(digitaldisplay_1_g), .f(digitaldisplay_1_f), .a(digitaldisplay_1_a), .b(digitaldisplay_1_b),
    .e(digitaldisplay_1_e), .d(digitaldisplay_1_d), .c(digitaldisplay_1_c));  // open: dp
  Multiplexer multiplexer_1 (.in0(fourbitadder_1_c0), .in1(1'b0), .out(multiplexer_1_out), .sel(Cout));
  Multiplexer multiplexer_2 (.in0(fourbitadder_1_c1), .in1(1'b0), .out(multiplexer_2_out), .sel(Cout));
  Multiplexer multiplexer_3 (.in0(fourbitadder_1_c2), .in1(1'b0), .out(multiplexer_3_out), .sel(Cout));
  Multiplexer multiplexer_4 (.in0(fourbitadder_1_c3), .in1(1'b0), .out(multiplexer_4_out), .sel(Cout));
endmodule

module decade (
  input  CLK,
  input  Set,
  input  Reset,
  input  Cin,
  output Q3,
  output Q2,
  output Q1,
  output Q0,
  output Cout
);

  wire fourbitadder_1_c0, fourbitadder_1_c1, fourbitadder_1_c2, fourbitadder_1_c3, multiplexer_1_out,
       multiplexer_2_out, multiplexer_3_out, multiplexer_4_out, not_1_out, not_2_out;

  fourbitDFF fourbitdff_1 (
    .D0(multiplexer_1_out), .D1(multiplexer_2_out), .D2(multiplexer_3_out), .D3(multiplexer_4_out),
    .CLK(CLK), .S(Set), .R(Reset), .Q0(Q0), .Q1(Q1), .Q2(Q2), .Q3(Q3));  // open: NQ0, NQ1, NQ2, NQ3
  fourbitadder fourbitadder_1 (
    .a0(Q0), .a1(Q1), .a2(Q2), .a3(Q3), .b0(1'b0), .b1(1'b0), .b2(1'b0), .b3(1'b0), .Cin(Cin),
    .c0(fourbitadder_1_c0), .c1(fourbitadder_1_c1), .c2(fourbitadder_1_c2), .c3(fourbitadder_1_c3));  // open: Cout
  not not_1 (not_1_out, fourbitadder_1_c0);
  not not_2 (not_2_out, fourbitadder_1_c3);
  and and_1 (Cout, not_1_out, fourbitadder_1_c1, fourbitadder_1_c2, not_2_out);
  Multiplexer multiplexer_1 (.in0(fourbitadder_1_c0), .out(multiplexer_1_out), .sel(Cout));  // open: in1
  Multiplexer multiplexer_2 (.in0(fourbitadder_1_c1), .out(multiplexer_2_out), .sel(Cout));  // open: in1
  Multiplexer multiplexer_3 (.in0(fourbitadder_1_c2), .out(multiplexer_3_out), .sel(Cout));  // open: in1
  Multiplexer multiplexer_4 (.in0(fourbitadder_1_c3), .out(multiplexer_4_out), .sel(Cout));  // open: in1
endmodule

module reunit (
  input  CLK,
  input  Set,
  input  Reset,
  input  Cin,
  output Q3,
  output Q2,
  output Q1,
  output Q0,
  output Cout
);

  wire digitaldisplay_1_a, digitaldisplay_1_b, digitaldisplay_1_c, digitaldisplay_1_d, digitaldisplay_1_e,
       digitaldisplay_1_f, digitaldisplay_1_g, fourbitadder_1_c0, fourbitadder_1_c1, fourbitadder_1_c2,
       fourbitadder_1_c3, multiplexer_1_out, multiplexer_2_out, multiplexer_3_out, multiplexer_4_out,
       not_1_out, not_2_out;

  fourbitDFF fourbitdff_1 (
    .D0(multiplexer_1_out), .D1(multiplexer_2_out), .D2(multiplexer_3_out), .D3(multiplexer_4_out),
    .CLK(CLK), .S(Set), .R(Reset), .Q0(Q0), .Q1(Q1), .Q2(Q2), .Q3(Q3));  // open: NQ0, NQ1, NQ2, NQ3
  fourbitadder fourbitadder_1 (
    .a0(Q0), .a1(Q1), .a2(Q2), .a3(Q3), .b0(1'b0), .b1(1'b0), .b2(1'b0), .b3(1'b0), .Cin(Cin),
    .c0(fourbitadder_1_c0), .c1(fourbitadder_1_c1), .c2(fourbitadder_1_c2), .c3(fourbitadder_1_c3));  // open: Cout
  digitaldisplay digitaldisplay_1 (
    .I0(Q0), .I1(Q1), .I2(Q2), .I3(Q3), .A(digitaldisplay_1_a), .B(digitaldisplay_1_b),
    .C(digitaldisplay_1_c), .D(digitaldisplay_1_d), .E(digitaldisplay_1_e), .F(digitaldisplay_1_f),
    .G(digitaldisplay_1_g));
  not not_1 (not_1_out, fourbitadder_1_c0);
  not not_2 (not_2_out, fourbitadder_1_c2);
  and and_1 (Cout, not_1_out, fourbitadder_1_c1, not_2_out, fourbitadder_1_c3);
  _7_Segment_Display u_7_segment_display_1 (
    .g(digitaldisplay_1_g), .f(digitaldisplay_1_f), .a(digitaldisplay_1_a), .b(digitaldisplay_1_b),
    .e(digitaldisplay_1_e), .d(digitaldisplay_1_d), .c(digitaldisplay_1_c));  // open: dp
  Multiplexer multiplexer_1 (.in0(fourbitadder_1_c0), .in1(1'b0), .out(multiplexer_1_out), .sel(Cout));
  Multiplexer multiplexer_2 (.in0(fourbitadder_1_c1), .in1(1'b0), .out(multiplexer_2_out), .sel(Cout));
  Multiplexer multiplexer_3 (.in0(fourbitadder_1_c2), .in1(1'b0), .out(multiplexer_3_out), .sel(Cout));
  Multiplexer multiplexer_4 (.in0(fourbitadder_1_c3), .in1(1'b0), .out(multiplexer_4_out), .sel(Cout));
endmodule
