// Logisim project full_adder.circ as structural Verilog: 2 circuits, main circuit fulladder
module fulladder (
  input  A,
  input  B,
  input  Cin,
  output result,
  output Cout
);

  wire halfadder_1_cout, halfadder_1_result, halfadder_2_cout;

  halfadder halfadder_1 (.Input0(A), .Input1(B), .result(halfadder_1_result), .Cout(halfadder_1_cout));
  halfadder halfadder_2 (.Input0(halfadder_1_result), .Input1(Cin), .result(result), .Cout(halfadder_2_cout));
  or or_1 (Cout, halfadder_2_cout, halfadder_1_cout);
endmodule

module halfadder (
  input  Input0,
  input  Input1,
  output result,
  output Cout
);

  and and_1 (Cout, Input0, Input1);
  xor xor_1 (result, Input0, Input1);
endmodule
