// Logisim project sequence_sum.circ as structural Verilog: 6 circuits, main circuit sequencesum
module sequencesum (
  input  Set,
  input  Reset,
  output a0,
  output a1,
  output a2,
  output a3,
  output a4,
  output a5,
  output a6,
  output a7
);

  wire clock_1_out, fourbitadder_1_cout, fourbitdff_1_q0, fourbitdff_1_q1, fourbitdff_1_q2, fourbitdff_1_q3,
       fourbitdff_2_q0, fourbitdff_2_q1, fourbitdff_2_q2, fourbitdff_2_q3, producenumber_1_o0,
       producenumber_1_o1, producenumber_1_o2, producenumber_1_o3;

  Clock clock_1 (.out(clock_1_out));
  fourbitDFF fourbitdff_1 (
    .D0(a0), .D1(a1), .D2(a2), .D3(a3), .CLK(clock_1_out), .S(Set), .R(Reset), .Q0(fourbitdff_1_q0),
    .Q1(fourbitdff_1_q1), .Q2(fourbitdff_1_q2), .Q3(fourbitdff_1_q3));  // open: NQ0, NQ1, NQ2, NQ3
  producenumber producenumber_1 (
    .CLK(clock_1_out), .S(Set), .R(Reset), .O0(producenumber_1_o0), .O1(producenumber_1_o1),
    .O2(producenumber_1_o2), .O3(producenumber_1_o3));
  fourbitDFF fourbitdff_2 (
    .D0(a4), .D1(a5), .D2(a6), .D3(a7), .CLK(clock_1_out), .S(Set), .R(Reset), .Q0(fourbitdff_2_q0),
    .Q1(fourbitdff_2_q1), .Q2(fourbitdff_2_q2), .Q3(fourbitdff_2_q3));  // open: NQ0, NQ1, NQ2, NQ3
  fourbitadder fourbitadder_1 (
    .a0(fourbitdff_1_q0), .a1(fourbitdff_1_q1), .a2(fourbitdff_1_q2), .a3(fourbitdff_1_q3),
    .b0(producenumber_1_o0), .b1(producenumber_1_o1), .b2(producenumber_1_o2), .b3(producenumber_1_o3),
    .Cin(1'b0), .c0(a0), .c1(a1), .c2(a2), .c3(a3), .Cout(fourbitadder_1_cout));
  fourbitadder fourbitadder_2 (
    .a0(fourbitdff_2_q0), .a1(fourbitdff_2_q1), .a2(fourbitdff_2_q2), .a3(fourbitdff_2_q3), .b0(1'b0),
    .b1(1'b0), .b2(1'b0), .b3(1'b0), .Cin(fourbitadder_1_cout), .c0(a4), .c1(a5), .c2(a6), .c3(a7));  // open: Cout
endmodule

module producenumber (
  input  CLK,
  input  S,
  input  R,
  output O0,
  output O1,
  output O2,
  output O3
);

  wire digitaldisplay_1_a, digitaldisplay_1_b, digitaldisplay_1_c, digitaldisplay_1_d, digitaldisplay_1_e,
       digitaldisplay_1_f, digitaldisplay_1_g, fourbitdff_1_q0, fourbitdff_1_q1, fourbitdff_1_q2,
       fourbitdff_1_q3, fulladder_1_cout, fulladder_2_cout, fulladder_3_cout;

  fourbitDFF fourbitdff_1 (
    .D0(O0), .D1(O1), .D2(O2), .D3(O3), .CLK(CLK), .S(S), .R(R), .Q0(fourbitdff_1_q0), .Q1(fourbitdff_1_q1),
    .Q2(fourbitdff_1_q2), .Q3(fourbitdff_1_q3));  // open: NQ0, NQ1, NQ2, NQ3
  fulladder fulladder_1 (.A(fourbitdff_1_q0), .B(1'b1), .Cin(1'b0), .result(O0), .Cout(fulladder_1_cout));
  fulladder fulladder_2 (.A(fourbitdff_1_q1), .B(1'b0), .Cin(fulladder_1_cout), .result(O1), .Cout(fulladder_2_cout));
  fulladder fulladder_3 (.A(fourbitdff_1_q2), .B(1'b0), .Cin(fulladder_2_cout), .result(O2), .Cout(fulladder_3_cout));
  fulladder fulladder_4 (.A(fourbitdff_1_q3), .B(1'b0), .Cin(fulladder_3_cout), .result(O3));  // open: Cout
  digitaldisplay digitaldisplay_1 (
    .I0(O0), .I1(O1), .I2(O2), .I3(O3), .A(digitaldisplay_1_a), .B(digitaldisplay_1_b),
    .C(digitaldisplay_1_c), .D(digitaldisplay_1_d), .E(digitaldisplay_1_e), .F(digitaldisplay_1_f),
    .G(digitaldisplay_1_g));
  _7_Segment_Display u_7_segment_display_1 (
    .g(digitaldisplay_1_g), .f(digitaldisplay_1_f), .a(digitaldisplay_1_a), .b(digitaldisplay_1_b),
    .e(digitaldisplay_1_e), .d(digitaldisplay_1_d), .c(digitaldisplay_1_c));  // open: dp
endmodule

module digitaldisplay (
  input  I0,
  input  I1,
  input  I2,
  input  I3,
  output A,
  output B,
  output C,
  output D,
  output E,
  output F,
  output G
);

  wire B0_out, B1_out, B2_out, B3_out, B4_out, B5_out, B6_out, B7_out, B8_out, B9_out, not_1_out, not_2_out,
       not_3_out, not_4_out;

  not not_1 (not_1_out, I0);
  not not_2 (not_2_out, I1);
  not not_3 (not_3_out, I2);
  not not_4 (not_4_out, I3);
  and B0 (B0_out, not_1_out, not_2_out, not_3_out, not_4_out);
  and B1 (B1_out, I0, not_2_out, not_3_out, not_4_out);
  and B2 (B2_out, not_1_out, I1, not_3_out, not_4_out);
  and B3 (B3_out, I0, I1, not_3_out, not_4_out);
  and B4 (B4_out, not_1_out, not_2_out, I2, not_4_out);
  and B5 (B5_out, I0, not_2_out, I2, not_4_out);
  and B6 (B6_out, not_1_out, I1, I2, not_4_out);
  and B7 (B7_out, I0, I1, I2, not_4_out);
  and B8 (B8_out, not_1_out, not_2_out, not_3_out, I3);
  and B9 (B9_out, I0, not_2_out, not_3_out, I3);
  or or_1 (A, B0_out, B2_out, B3_out, B5_out, B7_out, B8_out, B9_out);
  or or_2 (B, B0_out, B1_out, B2_out, B3_out, B4_out, B7_out, B8_out, B9_out);
  or or_3 (C, B0_out, B1_out, B3_out, B4_out, B5_out, B6_out, B7_out, B8_out, B9_out);
  or or_4 (D, B0_out, B2_out, B3_out, B5_out, B6_out, B8_out);
  or or_5 (E, B0_out, B2_out, B6_out, B8_out);
  or or_6 (F, B0_out, B4_out, B5_out, B6_out, B8_out, B9_out);
  or or_7 (G, B2_out, B3_out, B4_out, B5_out, B6_out, B8_out, B9_out);
  _7_Segment_Display u_7_segment_display_1 (.g(G), .f(F), .a(A), .b(B), .e(E), .d(D), .c(C));  // open: dp
endmodule

module fourbitDFF (
  input  D0,
  input  D1,
  input  D2,
  input  D3,
  input  CLK,
  input  S,
  input  R,
  output Q0,
  output Q1,
  output Q2,
  output Q3,
  output NQ0,
  output NQ1,
  output NQ2,
  output NQ3
);

  D_Flip_Flop d_ff_1 (.D(D0), .clk(CLK), .Q(Q0), .Qn(NQ0), .preset(S), .reset(R));
  D_Flip_Flop d_ff_2 (.D(D1), .clk(CLK), .Q(Q1), .Qn(NQ1), .preset(S), .reset(R));
  D_Flip_Flop d_ff_3 (.D(D2), .clk(CLK), .Q(Q2), .Qn(NQ2), .preset(S), .reset(R));
  D_Flip_Flop d_ff_4 (.D(D3), .clk(CLK), .Q(Q3), .Qn(NQ3), .preset(S), .reset(R));
endmodule

module tendisplay (
  input  a0,
  input  a1,
  input  a2,
  input  a3,
  input  Cin,
  output b0,
  output b1,
  output b2,
  output b3,
  output Cout
);

  wire and_1_out, and_2_out, and_3_out, fulladder_1_cout, fulladder_2_cout, fulladder_2_result,
       fulladder_3_cout, fulladder_3_result, fulladder_4_cout, fulladder_4_result, not_2_out, not_3_out,
       not_4_out, or_1_out, or_3_out;

  fulladder fulladder_1 (.A(a0), .B(1'b0), .Cin(Cin), .result(b0), .Cout(fulladder_1_cout));
  fulladder fulladder_2 (
    .A(a1), .B(1'b0), .Cin(fulladder_1_cout), .result(fulladder_2_result), .Cout(fulladder_2_cout));
  fulladder fulladder_3 (
    .A(a2), .B(1'b0), .Cin(fulladder_2_cout), .result(fulladder_3_result), .Cout(fulladder_3_cout));
  fulladder fulladder_4 (
    .A(a3), .B(1'b0), .Cin(fulladder_3_cout), .result(fulladder_4_result), .Cout(fulladder_4_cout));
  // NOT_Gate not_1 has open pins: in=b0, out=open
  not not_2 (not_2_out, fulladder_2_result);
  not not_3 (not_3_out, fulladder_3_result);
  not not_4 (not_4_out, fulladder_4_result);
  or or_1 (or_1_out, fulladder_2_result, fulladder_3_result);
  and and_1 (and_1_out, or_1_out, fulladder_4_result);
  or or_2 (Cout, fulladder_4_cout, and_1_out);
  and and_2 (and_2_out, not_4_out, fulladder_2_result);
  and and_3 (and_3_out, not_2_out, fulladder_3_result, fulladder_4_result);
  or or_3 (or_3_out, fulladder_2_result, not_4_out);
  and and_4 (b2, or_3_out, fulladder_3_result);
  and and_5 (b3, not_2_out, not_3_out, fulladder_4_result);
  or or_4 (b1, and_2_out, and_3_out);
endmodule

module fourbitadder (
  input  a0,
  input  a1,
  input  a2,
  input  a3,
  input  b0,
  input  b1,
  input  b2,
  input  b3,
  input  Cin,
  output c0,
  output c1,
  output c2,
  output c3,
  output Cout
);

  wire fulladder_1_cout, fulladder_2_cout, fulladder_3_cout;

  fulladder fulladder_1 (.A(a0), .B(b0), .Cin(Cin), .result(c0), .Cout(fulladder_1_cout));
  fulladder fulladder_2 (.A(a1), .B(b1), .Cin(fulladder_1_cout), .result(c1), .Cout(fulladder_2_cout));
  fulladder fulladder_3 (.A(a2), .B(b2), .Cin(fulladder_2_cout), .result(c2), .Cout(fulladder_3_cout));
  fulladder fulladder_4 (.A(a3), .B(b3), .Cin(fulladder_3_cout), .result(c3), .Cout(Cout));
endmodule
