// Logisim project seven_segment_digital_tube_decoders.circ as structural Verilog: 1 circuit, main circuit sevensegment
module sevensegment (
  input  a0,
  input  a1,
  input  a2,
  input  a3,
  output A,
  output B,
  output C,
  output D,
  output E,
  output F,
  output G
);

  wire b0_out, b1_out, b2_out, b3_out, b4_out, b5_out, b6_out, b7_out, b8_out, b9_out, b10_out, b11_out,
       b12_out, b13_out, b14_out, b15_out, not_1_out, not_2_out, not_3_out, not_4_out;

  not not_1 (not_1_out, a0);
  not not_2 (not_2_out, a1);
  not not_3 (not_3_out, a2);
  not not_4 (not_4_out, a3);
  and b0 (b0_out, not_1_out, not_2_out, not_3_out, not_4_out);
  and b1 (b1_out, a0, not_2_out, not_3_out, not_4_out);
  and b2 (b2_out, not_1_out, a1, not_3_out, not_4_out);
  and b3 (b3_out, a0, a1, not_3_out, not_4_out);
  and b4 (b4_out, not_1_out, not_2_out, a2, not_4_out);
  and b5 (b5_out, a0, not_2_out, a2, not_4_out);
  and b6 (b6_out, not_1_out, a1, a2, not_4_out);
  and b7 (b7_out, a0, a1, a2, not_4_out);
  and b8 (b8_out, not_1_out, not_2_out, not_3_out, a3);
  and b9 (b9_out, a0, not_2_out, not_3_out, a3);
  and b10 (b10_out, not_1_out, a1, not_3_out, a3);
  and b11 (b11_out, a0, a1, not_3_out, a3);
  and b12 (b12_out, not_1_out, not_2_out, a2, a3);
  and b13 (b13_out, a0, not_2_out, a2, a3);
  and b14 (b14_out, not_1_out, a1, a2, a3);
  and b15 (b15_out, a0, a1, a2, a3);
  or or_1 (A, b0_out, b2_out, b3_out, b5_out, b6_out, b7_out, b8_out, b9_out, b10_out, b12_out, b14_out, b15_out);
  or or_2 (B, b0_out, b1_out, b2_out, b3_out, b4_out, b7_out, b8_out, b9_out, b10_out, b13_out);
  or or_3 (C, b0_out, b1_out, b3_out, b4_out, b5_out, b6_out, b7_out, b8_out, b9_out, b10_out, b11_out, b13_out);
  or or_4 (D, b0_out, b2_out, b3_out, b5_out, b6_out, b8_out, b9_out, b11_out, b12_out, b13_out, b14_out);
  or or_5 (E, b10_out, b0_out, b2_out, b6_out, b8_out, b11_out, b12_out, b14_out, b15_out, b13_out);
  or or_6 (F, b0_out, b4_out, b5_out, b6_out, b8_out, b9_out, b10_out, b11_out, b12_out, b14_out, b15_out);
  or or_7 (G, b2_out, b3_out, b4_out, b5_out, b6_out, b8_out, b9_out, b10_out, b11_out, b13_out, b14_out, b15_out);
endmodule
