// Logisim project seven_segment_display_with_switchable_carry_counting_system.circ as structural Verilog: 1 circuit, main circuit main
module main (
  input  I0,
  input  I1,
  input  I2,
  input  I3,
  input  S
);

  wire a_out, and_1_out, and_2_out, and_3_out, and_4_out, and_5_out, and_6_out, and_7_out, and_8_out,
       and_9_out, and_10_out, and_11_out, and_12_out, b0_out, b1_out, b2_out, b3_out, b4_out, b5_out, b6_out,
       b7_out, b8_out, b9_out, b10_out, b11_out, b12_out, b13_out, b14_out, b15_out, b_out, c_out, d_out,
       e_out, f_out, g_out, not_1_out, not_2_out, not_3_out, not_4_out, not_5_out, or_1_out, or_2_out,
       or_3_out, or_4_out, or_5_out, or_6_out;

  not not_1 (not_1_out, I0);
  not not_2 (not_2_out, I1);
  not not_3 (not_3_out, I2);
  not not_4 (not_4_out, I3);
  and b0 (b0_out, not_1_out, not_2_out, not_3_out, not_4_out);
  and b1 (b1_out, I0, not_2_out, not_3_out, not_4_out);
  and b2 (b2_out, not_1_out, I1, not_3_out, not_4_out);
  and b3 (b3_out, I0, I1, not_3_out, not_4_out);
  and b4 (b4_out, not_1_out, not_2_out, I2, not_4_out);
  and b5 (b5_out, I0, not_2_out, I2, not_4_out);
  and b6 (b6_out, not_1_out, I1, I2, not_4_out);
  and b7 (b7_out, I0, I1, I2, not_4_out);
  and b8 (b8_out, not_1_out, not_2_out, not_3_out, I3);
  and b9 (b9_out, I0, not_2_out, not_3_out, I3);
  and b10 (b10_out, not_1_out, I1, not_3_out, I3);
  and b11 (b11_out, I0, I1, not_3_out, I3);
  and b12 (b12_out, not_1_out, not_2_out, I2, I3);
  and b13 (b13_out, I0, not_2_out, I2, I3);
  and b14 (b14_out, not_1_out, I1, I2, I3);
  and b15 (b15_out, I0, I1, I2, I3);
  not not_5 (not_5_out, S);
  and and_1 (and_1_out, b10_out, not_5_out);
  and and_2 (and_2_out, not_5_out, b11_out);
  and and_3 (and_3_out, not_5_out, b12_out);
  and and_4 (and_4_out, not_5_out, b13_out);
  and and_5 (and_5_out, b14_out, not_5_out);
  and and_6 (and_6_out, b15_out, not_5_out);
  and and_7 (and_7_out, b10_out, S);
  and and_8 (and_8_out, b11_out, S);
  and and_9 (and_9_out, b12_out, S);
  or or_1 (or_1_out, b0_out, and_1_out);
  or or_2 (or_2_out, b1_out, and_2_out);
  or or_3 (or_3_out, b2_out, and_3_out);
  or or_4 (or_4_out, b3_out, and_4_out);
  or or_5 (or_5_out, b4_out, and_5_out);
  or or_6 (or_6_out, b5_out, and_6_out);
  and and_10 (and_10_out, b13_out, S);
  and and_11 (and_11_out, b14_out, S);
  and and_12 (and_12_out, b15_out, S);
  or a (a_out, or_1_out, or_3_out, or_4_out, or_6_out, b6_out, b7_out, b8_out, b9_out, and_7_out, and_9_out, and_11_out, and_12_out);
  or b (b_out, or_1_out, or_2_out, or_3_out, or_4_out, or_5_out, b7_out, b8_out, b9_out, and_7_out, and_10_out);
  or c (c_out, or_1_out, or_2_out, or_4_out, or_5_out, or_6_out, b6_out, b7_out, b8_out, b9_out, and_7_out, and_8_out, and_10_out);
  or d (d_out, or_1_out, or_3_out, or_4_out, or_6_out, b6_out, b8_out, b9_out, and_8_out, and_9_out, and_10_out, and_11_out);
  or e (e_out, and_7_out, or_1_out, or_3_out, b6_out, b8_out, and_8_out, and_9_out, and_11_out, and_12_out, and_10_out);
  or f (f_out, or_1_out, or_5_out, or_6_out, b6_out, b8_out, b9_out, and_7_out, and_8_out, and_9_out, and_11_out, and_12_out);
  or g (g_out, or_3_out, or_4_out, or_5_out, or_6_out, b6_out, b8_out, b9_out, and_7_out, and_8_out, and_10_out, and_11_out, and_12_out);
  _7_Segment_Display u_7_segment_display_1 (
    .g(g_out), .f(f_out), .a(a_out), .b(b_out), .e(e_out), .d(d_out), .c(c_out));  // open: dp
endmodule
