// Logisim project simple_CPU.circ as structural Verilog: 2 circuits, main circuit sCPU
module sCPU (
  input  reset1,
  input  reset2,
  output [7:0] r0,
  output [7:0] r1,
  output [7:0] r2,
  output [7:0] r3,
  output wen,
  output [1:0] waddr,
  output [7:0] wdata,
  output [1:0] raddr1,
  output [1:0] raddr2,
  output take
);

  wire clk_out, comparator_1_eq, comparator_2_eq, comparator_3_eq, comparator_4_eq, comparator_5_eq,
       not_1_out;
  wire [1:0] multiplexer_2_out;
  wire [3:0] adder_1_out, multiplexer_1_out, register_1_q;
  wire [3:2] multiplexer_2_out_2;
  wire [7:0] adder_2_out, gpr_4x8_2w1r_1_rdata1, gpr_4x8_2w1r_1_rdata2, register_2_q;

  Clock clk (.out(clk_out));
  Register #(.width(4)) register_1 (.D(multiplexer_1_out), .en(1'b1), .clk(clk_out), .Q(register_1_q), .clr(reset1));
  Multiplexer #(.width(4)) multiplexer_1 (
    .in0(adder_1_out), .in1({waddr, multiplexer_2_out_2}), .out(multiplexer_1_out), .sel(take));
  Multiplexer #(.select(4), .width(8)) multiplexer_2 (
    .in0(8'h8a), .in1(8'h90), .in2(8'ha0), .in3(8'hb1), .in4(8'h17), .in5(8'h29), .in6(8'hd1), .in7(8'h42),
    .in8(8'he3), .out({multiplexer_2_out, waddr, multiplexer_2_out_2, raddr2}), .sel(register_1_q));  // open: in9, in10, in11, in12, in13, in14, in15
  Adder #(.width(4)) adder_1 (.a(register_1_q), .b(4'b0001), .out(adder_1_out));  // open: cin, cout
  Comparator #(.width(2)) comparator_1 (.a(multiplexer_2_out), .b(2'b10), .eq(comparator_1_eq));  // open: gt, lt
  Comparator #(.width(2)) comparator_2 (.a(multiplexer_2_out), .b(2'b00), .eq(comparator_2_eq));  // open: gt, lt
  Comparator #(.width(2)) comparator_3 (.a(multiplexer_2_out), .b(2'b11), .eq(comparator_3_eq));  // open: gt, lt
  Comparator #(.width(2)) comparator_4 (.a(multiplexer_2_out), .b(2'b01), .eq(comparator_4_eq));  // open: gt, lt
  or or_1 (wen, comparator_1_eq, comparator_2_eq);
  Multiplexer #(.width(2)) multiplexer_3 (.in0(multiplexer_2_out_2), .in1(2'b00), .out(raddr1), .sel(comparator_3_eq));
  Register register_2 (.D(gpr_4x8_2w1r_1_rdata2), .en(comparator_4_eq), .clk(clk_out), .Q(register_2_q), .clr(reset2));
  Multiplexer #(.width(8)) multiplexer_4 (
    .in0({4'b0000, multiplexer_2_out_2, raddr2}), .in1(adder_2_out), .out(wdata), .sel(comparator_2_eq));
  and and_1 (take, comparator_3_eq, not_1_out);
  Hex_Digit_Display hex_digit_display_1 (.value(register_2_q[7:4]));  // open: dp
  Hex_Digit_Display hex_digit_display_2 (.value(register_2_q[3:0]));  // open: dp
  GPR_4x8_2W1R gpr_4x8_2w1r_1 (
    .clk(clk_out), .wen(wen), .waddr(waddr), .wdata(wdata), .raddr1(raddr1), .raddr2(raddr2),
    .rdata1(gpr_4x8_2w1r_1_rdata1), .rdata2(gpr_4x8_2w1r_1_rdata2), .q0(r0), .q1(r1), .q2(r2), .q3(r3));
  Adder adder_2 (.a(gpr_4x8_2w1r_1_rdata1), .b(gpr_4x8_2w1r_1_rdata2), .out(adder_2_out));  // open: cin, cout
  Comparator comparator_5 (.a(gpr_4x8_2w1r_1_rdata1), .b(gpr_4x8_2w1r_1_rdata2), .eq(comparator_5_eq));  // open: gt, lt
  not not_1 (not_1_out, comparator_5_eq);
endmodule

module GPR_4x8_2W1R (
  input  clk,
  input  wen,
  input  [1:0] waddr,
  input  [7:0] wdata,
  input  [1:0] raddr1,
  input  [1:0] raddr2,
  output [7:0] rdata1,
  output [7:0] rdata2,
  output [7:0] q0,
  output [7:0] q1,
  output [7:0] q2,
  output [7:0] q3
);

  wire and_1_out, and_2_out, and_3_out, and_4_out, decoder_1_out0, decoder_1_out1, decoder_1_out2,
       decoder_1_out3;

  Register r0 (.D(wdata), .en(and_1_out), .clk(clk), .Q(q0));  // open: clr
  Register r1 (.D(wdata), .en(and_2_out), .clk(clk), .Q(q1));  // open: clr
  Register r2 (.D(wdata), .en(and_3_out), .clk(clk), .Q(q2));  // open: clr
  Register r3 (.D(wdata), .en(and_4_out), .clk(clk), .Q(q3));  // open: clr
  Decoder #(.enable("false"), .select(2)) decoder_1 (
    .out0(decoder_1_out0), .out1(decoder_1_out1), .out2(decoder_1_out2), .out3(decoder_1_out3), .sel(waddr));
  and and_1 (and_1_out, wen, decoder_1_out0);
  and and_2 (and_2_out, decoder_1_out1, wen);
  and and_3 (and_3_out, decoder_1_out2, wen);
  and and_4 (and_4_out, decoder_1_out3, wen);
  Multiplexer #(.select(2), .width(8)) multiplexer_1 (
    .in0(q0), .in1(q1), .in2(q2), .in3(q3), .out(rdata1), .sel(raddr1));
  Multiplexer #(.select(2), .width(8)) multiplexer_2 (
    .in0(q0), .in1(q1), .in2(q2), .in3(q3), .out(rdata2), .sel(raddr2));
endmodule
