// Logisim project GPR.circ as structural Verilog: 1 circuit, main circuit GPR
module GPR (
  input  clk,
  input  [31:0] wdata,
  input  wen,
  input  [3:0] waddr,
  input  [3:0] raddr1,
  input  [3:0] raddr2,
  input  reset,
  output [31:0] rdata1,
  output [31:0] rdata2
);

  wire decoder_1_out1, decoder_1_out2, decoder_1_out3, decoder_1_out4, decoder_1_out5, decoder_1_out6,
       decoder_1_out7, decoder_1_out8, decoder_1_out9, decoder_1_out10, decoder_1_out11, decoder_1_out12,
       decoder_1_out13, decoder_1_out14, decoder_1_out15;
  wire [31:0] x0_q, x1_q, x2_q, x3_q, x4_q, x5_q, x6_q, x7_q, x8_q, x9_q, x10_q, x11_q, x12_q, x13_q, x14_q,
       x15_q;

  Decoder #(.select(4)) decoder_1 (
    .out1(decoder_1_out1), .out2(decoder_1_out2), .out3(decoder_1_out3), .out4(decoder_1_out4),
    .out5(decoder_1_out5), .out6(decoder_1_out6), .out7(decoder_1_out7), .out8(decoder_1_out8),
    .out9(decoder_1_out9), .out10(decoder_1_out10), .out11(decoder_1_out11), .out12(decoder_1_out12),
    .out13(decoder_1_out13), .out14(decoder_1_out14), .out15(decoder_1_out15), .sel(waddr), .en(wen));  // open: out0
  Register #(.width(32)) x0 (.D(wdata), .en(1'b0), .clk(clk), .Q(x0_q), .clr(reset));
  Register #(.width(32)) x8 (.D(wdata), .en(decoder_1_out8), .clk(clk), .Q(x8_q), .clr(reset));
  Register #(.width(32)) x1 (.D(wdata), .en(decoder_1_out1), .clk(clk), .Q(x1_q), .clr(reset));
  Register #(.width(32)) x9 (.D(wdata), .en(decoder_1_out9), .clk(clk), .Q(x9_q), .clr(reset));
  Register #(.width(32)) x2 (.D(wdata), .en(decoder_1_out2), .clk(clk), .Q(x2_q), .clr(reset));
  Register #(.width(32)) x10 (.D(wdata), .en(decoder_1_out10), .clk(clk), .Q(x10_q), .clr(reset));
  Register #(.width(32)) x3 (.D(wdata), .en(decoder_1_out3), .clk(clk), .Q(x3_q), .clr(reset));
  Register #(.width(32)) x11 (.D(wdata), .en(decoder_1_out11), .clk(clk), .Q(x11_q), .clr(reset));
  Register #(.width(32)) x4 (.D(wdata), .en(decoder_1_out4), .clk(clk), .Q(x4_q), .clr(reset));
  Register #(.width(32)) x12 (.D(wdata), .en(decoder_1_out12), .clk(clk), .Q(x12_q), .clr(reset));
  Register #(.width(32)) x5 (.D(wdata), .en(decoder_1_out5), .clk(clk), .Q(x5_q), .clr(reset));
  Register #(.width(32)) x13 (.D(wdata), .en(decoder_1_out13), .clk(clk), .Q(x13_q), .clr(reset));
  Register #(.width(32)) x6 (.D(wdata), .en(decoder_1_out6), .clk(clk), .Q(x6_q), .clr(reset));
  Register #(.width(32)) x14 (.D(wdata), .en(decoder_1_out14), .clk(clk), .Q(x14_q), .clr(reset));
  Register #(.width(32)) x7 (.D(wdata), .en(decoder_1_out7), .clk(clk), .Q(x7_q), .clr(reset));
  Register #(.width(32)) x15 (.D(wdata), .en(decoder_1_out15), .clk(clk), .Q(x15_q), .clr(reset));
  Multiplexer #(.select(4), .width(32)) multiplexer_1 (
    .in0({32{1'b0}}), .in1(x1_q), .in2(x2_q), .in3(x3_q), .in4(x4_q), .in5(x5_q), .in6(x6_q), .in7(x7_q),
    .in8(x8_q), .in9(x9_q), .in10(x10_q), .in11(x11_q), .in12(x12_q), .in13(x13_q), .in14(x14_q),
    .in15(x15_q), .out(rdata1), .sel(raddr1));
  Multiplexer #(.select(4), .width(32)) multiplexer_2 (
    .in0({32{1'b0}}), .in1(x1_q), .in2(x2_q), .in3(x3_q), .in4(x4_q), .in5(x5_q), .in6(x6_q), .in7(x7_q),
    .in8(x8_q), .in9(x9_q), .in10(x10_q), .in11(x11_q), .in12(x12_q), .in13(x13_q), .in14(x14_q),
    .in15(x15_q), .out(rdata2), .sel(raddr2));
endmodule
