// Logisim project RISCV.circ as structural Verilog: 7 circuits, main circuit RISC_V
module RISC_V (
  input  reset,
  output [31:0] pc,
  output [31:0] inst,
  output [31:0] eff_addr,
  output is_sw,
  output isVGA,
  output VGA_WE,
  output isRAM,
  output [31:0] out_9
);

  wire and_1_out, clk_out, decodecore_1_is_add, decodecore_1_is_addi, decodecore_1_is_jalr,
       decodecore_1_is_lbu, decodecore_1_is_lui, decodecore_1_is_lw, decodecore_1_is_sb, execcore_1_gpr_wen,
       execcore_1_pc_sel, memaccessif_1_mem_gpr_wen, memaccessif_1_ram_wen, or_1_out, or_2_out;
  wire [3:0] decodecore_1_rd4, decodecore_1_rs1_4, decodecore_1_rs2_4, execcore_1_waddr,
       memaccessif_1_mem_waddr, memaccessif_1_ram_be, multiplexer_1_out;
  wire [17:0] memaccessif_1_ram_addr;
  wire [23:0] gpr_1_rdata2;
  wire [31:0] decodecore_1_immi32, decodecore_1_imms32, decodecore_1_immu32, execcore_1_pc_target,
       execcore_1_wdata, fetch_1_pc_plus4, gpr_1_rdata1, memaccessif_1_mem_wdata, memaccessif_1_ram_wdata,
       multiplexer_2_out, ram_1_dout;
  wire [31:24] gpr_1_rdata2_2;
  wire [63:32] cyclecounter64_1_count;

  Clock clk (.out(clk_out));
  or or_1 (or_1_out, execcore_1_gpr_wen, memaccessif_1_mem_gpr_wen);
  CycleCounter64 cyclecounter64_1 (.clk(clk_out), .reset(reset), .en(1'b1), .count({cyclecounter64_1_count, out_9}));
  Fetch fetch_1 (
    .clk(clk_out), .wen(1'b1), .reset(reset), .pc_target(execcore_1_pc_target), .pc_sel(execcore_1_pc_sel),
    .pc(pc), .pc_plus4(fetch_1_pc_plus4), .inst(inst));
  GPR gpr_1 (
    .clk(clk_out), .wdata(multiplexer_2_out), .wen(or_1_out), .waddr(multiplexer_1_out),
    .raddr1(decodecore_1_rs1_4), .raddr2(decodecore_1_rs2_4), .reset(reset), .rdata1(gpr_1_rdata1),
    .rdata2({gpr_1_rdata2_2, gpr_1_rdata2}));
  ExecCore execcore_1 (
    .pc_plus4(fetch_1_pc_plus4), .rdata1(gpr_1_rdata1), .rd4(decodecore_1_rd4), .immI32(decodecore_1_immi32),
    .is_addi(decodecore_1_is_addi), .is_jalr(decodecore_1_is_jalr), .rdata2({gpr_1_rdata2_2, gpr_1_rdata2}),
    .is_add(decodecore_1_is_add), .is_lui(decodecore_1_is_lui), .immU32(decodecore_1_immu32),
    .gpr_wen(execcore_1_gpr_wen), .waddr(execcore_1_waddr), .wdata(execcore_1_wdata),
    .pc_sel(execcore_1_pc_sel), .pc_target(execcore_1_pc_target));
  DecodeCore decodecore_1 (
    .inst(inst), .rd4(decodecore_1_rd4), .rs1_4(decodecore_1_rs1_4), .immI32(decodecore_1_immi32),
    .is_addi(decodecore_1_is_addi), .is_jalr(decodecore_1_is_jalr), .rs2_4(decodecore_1_rs2_4),
    .immU32(decodecore_1_immu32), .is_add(decodecore_1_is_add), .is_lui(decodecore_1_is_lui),
    .immS32(decodecore_1_imms32), .is_lw(decodecore_1_is_lw), .is_sw(is_sw), .is_lbu(decodecore_1_is_lbu),
    .is_sb(decodecore_1_is_sb));  // open: opcode, funct3, func7
  Multiplexer #(.width(4)) multiplexer_1 (
    .in0(execcore_1_waddr), .in1(memaccessif_1_mem_waddr), .out(multiplexer_1_out), .sel(or_2_out));
  Multiplexer #(.width(32)) multiplexer_2 (
    .in0(execcore_1_wdata), .in1(memaccessif_1_mem_wdata), .out(multiplexer_2_out), .sel(or_2_out));
  MemAccessIF memaccessif_1 (
    .rd4(decodecore_1_rd4), .rdata1(gpr_1_rdata1), .rdata2({gpr_1_rdata2_2, gpr_1_rdata2}),
    .immI32(decodecore_1_immi32), .immS32(decodecore_1_imms32), .is_lw(decodecore_1_is_lw), .is_sw(is_sw),
    .ram_rdata(ram_1_dout), .is_lbu(decodecore_1_is_lbu), .is_sb(decodecore_1_is_sb),
    .mem_gpr_wen(memaccessif_1_mem_gpr_wen), .mem_waddr(memaccessif_1_mem_waddr),
    .mem_wdata(memaccessif_1_mem_wdata), .ram_addr(memaccessif_1_ram_addr), .ram_wen(memaccessif_1_ram_wen),
    .ram_be(memaccessif_1_ram_be), .ram_wdata(memaccessif_1_ram_wdata), .eff_addr(eff_addr));
  or or_2 (or_2_out, decodecore_1_is_lw, decodecore_1_is_lbu);
  and and_1 (and_1_out, memaccessif_1_ram_wen, isRAM);
  RAM #(.addrWidth(18), .asyncread("true"), .byteenables("byteEnables"), .dataWidth(32)) ram_1 (
    .addr(memaccessif_1_ram_addr), .we(and_1_out), .oe(isRAM), .clk(clk_out), .din(memaccessif_1_ram_wdata),
    .dout(ram_1_dout), .be3(memaccessif_1_ram_be[3]), .be2(memaccessif_1_ram_be[2]),
    .be1(memaccessif_1_ram_be[1]), .be0(memaccessif_1_ram_be[0]));
  // RGB_Video #(.cursor("No Cursor"), .height(256), .width(256)) rgb_video_1: pin names not known; wires that end beside it: reset, clk_out, VGA_WE, eff_addr[9:2], eff_addr[17:10], gpr_1_rdata2
  Comparator #(.width(14)) comparator_1 (.a(eff_addr[31:18]), .b(14'h800), .eq(isVGA));  // open: gt, lt
  Comparator #(.width(12)) comparator_2 (.a(eff_addr[31:20]), .b({12{1'b0}}), .eq(isRAM));  // open: gt, lt
  and and_2 (VGA_WE, is_sw, isVGA);
endmodule

module Fetch (
  input  clk,
  input  wen,
  input  reset,
  input  [31:0] pc_target,
  input  pc_sel,
  output [31:0] pc,
  output [31:0] pc_plus4,
  output [31:0] inst
);

  wire [31:0] multiplexer_1_out;

  Register #(.width(32)) register_1 (.D(multiplexer_1_out), .en(wen), .clk(clk), .Q(pc), .clr(reset));
  Adder #(.width(32)) adder_1 (.a(pc), .b(32'h4), .out(pc_plus4));  // open: cin, cout
  Multiplexer #(.width(32)) multiplexer_1 (.in0(pc_plus4), .in1(pc_target), .out(multiplexer_1_out), .sel(pc_sel));
  ROM #(.addrWidth(18), .dataWidth(32)) rom_1 (.addr(pc[19:2]), .data(inst));

  // Notes on the sheet:
  //   contents of rom_1 (hex, n*v repeats v):
  //   413 93137 10113 10b7 dbc08093 80e7 fe012823 fea10923 fea12423 fe914203 fe4109a3 ff012783 f787b3
  //   f787b3 4b6b7 f0068693 fdc10113 d787b3 10000713 f12423 10593 100793 b00513 2112023 12023 12223 e12623
  //   e12823 f10a23 10b7 a8408093 80e7 2012083 2410113 8067 ff410113 112423 10b7 a7c08093 80e7 513 1800093
  //   80e7 812083 513 c10113 8067 852583 feb12823 fe812e23 3437 a0840413 ff014183 3401b3 1c183 ff114203
  //   440233 24203 4181b3 ff214203 440233 24203 4181b3 ff314203 440233 24203 4181b3 3237 a0020213 320233
  //   24203 ffc12403 420233 420233 410233 11b7 85c18193 fe312823 14800193 fe312623 fec22203 20067 1052703
  //   52683 452783 fe810113 e12423 112a23 fed12823 fef12623 13737 c0070713 fe012223 ff314203 fe4102a3
  //   fef14203 fe410223 fe412203 470233 24203 fe4105a3 ff214203 fe4102a3 fee14203 fe410223 fe412203 470233
  //   24203 fe410523 ff114203 fe4102a3 fed14203 fe410223 fe412203 470233 24203 fe4104a3 ff014203 fe4102a3
  //   fec14203 fe410223 fe412203 470233 24203 fe410423 fe812703 c52603 fee12823 fe812e23 3437 a0840413
  //   ff014183 3401b3 1c183 ff114203 440233 24203 4181b3 ff214203 440233 24203 4181b3 ff314203 440233
  //   24203 4181b3 3237 a0020213 320233 24203 ffc12403 420233 420233 410233 66800193 fe312823 28000193
  //   fe312623 fec22203 20067 c68733 10000513 fe812e23 fe912c23 fee12823 50413 ff012483 fe812423 feb14183
  //   3181b3 fe312423 fe914183 3181b3 fe912423 feb14203 420233 fe412423 fe914203 4181b3 3181b3 fe312a23
  //   fe912423 33237 b0020213 feb14183 4181b3 1c183 fe3103a3 fea14183 4181b3 1c183 fe310323 fe914183
  //   4181b3 1c183 fe3102a3 fe814183 4181b3 1c183 fe310223 ff412183 fe412203 440233 120213 fe412423
  //   feb14203 420233 fe412423 fe914203 4181b3 3237 b0820213 320233 ff812483 ffc12403 24203 420233 420233
  //   410233 11b7 86018193 fe312823 38800193 fe312623 fec22203 20067 812703 10000513 812823 e78733
  //   fe812e23 fe912c23 fee12823 50413 ff012483 fe812423 feb14183 3181b3 fe312423 fe914183 3181b3 fe912423
  //   feb14203 420233 fe412423 fe914203 4181b3 3181b3 fe312a23 fe912423 33237 b0020213 feb14183 4181b3
  //   1c183 fe3103a3 fea14183 4181b3 1c183 fe310323 fe914183 4181b3 1c183 fe3102a3 fe814183 4181b3 1c183
  //   fe310223 ff412183 fe412203 440233 120213 fe412423 feb14203 420233 fe412423 fe914203 4181b3 3237
  //   b0820213 320233 ff812483 ffc12403 24203 420233 420233 410233 11b7 86418193 fe312823 49800193
  //   fe312623 fec22203 20067 8*f787b3 d787b3 f787b3 f787b3 20000437 f40433 812783 c60633 c60633 fef12423
  //   feb14183 3181b3 fe312423 fe914183 fff78213 fe412423 feb14203 420233 fe412423 fe914203 4181b3 3237
  //   b1820213 418233 24203 420233 420233 410233 65800193 fe312823 53c00193 fe312623 fec22203 20067 912623
  //   493 40513 c12223 b12023 10b7 de008093 80e7 12583 412603 812783 148493 40040413 c585b3 fef12823
  //   fe912623 fe812e23 fe912c23 4b437 d0040413 ff014183 340233 100193 320023 fec14183 3401b3 18023 24183
  //   ff114483 940233 100493 920023 fed14483 9404b3 48023 24483 9181b3 ff214483 940233 100493 920023
  //   fee14483 9404b3 48023 24483 9181b3 ff314483 940233 100493 920023 fef14483 9404b3 48023 24483 9181b3
  //   3237 a0020213 320233 24203 ff812483 ffc12403 420233 420233 410233 65400193 fe312823 54400193
  //   fe312623 fec22203 20067 c12483 1012403 1412083 1810113 8067 10000713 fec12823 fee12623 fe812e23
  //   fe912c23 4b437 d0040413 ff014183 340233 100193 320023 fec14183 3401b3 18023 24183 ff114483 940233
  //   100493 920023 fed14483 9404b3 48023 24483 9181b3 ff214483 940233 100493 920023 fee14483 9404b3 48023
  //   24483 9181b3 ff314483 940233 100493 920023 fef14483 9404b3 48023 24483 9181b3 3237 a0020213 320233
  //   24203 ff812483 ffc12403 420233 420233 410233 74c00193 fe312823 28000193 fe312623 fec22203 20067
  //   812703 fee12823 fec12623 fe812e23 fe912c23 4b437 d0040413 ff014183 340233 100193 320023 fec14183
  //   3401b3 18023 24183 ff114483 940233 100493 920023 fed14483 9404b3 48023 24483 9181b3 ff214483 940233
  //   100493 920023 fee14483 9404b3 48023 24483 9181b3 ff314483 940233 100493 920023 fef14483 9404b3 48023
  //   24483 9181b3 3237 a0020213 320233 24203 ff812483 ffc12403 420233 420233 410233 11b7 83418193
  //   fe312823 38800193 fe312623 fec22203 20067 1412083 40637 20000537 1810113 1237 de020213 20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
endmodule

module ExecIJ (
  input  [31:0] pc_plus4,
  input  [31:0] rdata1,
  input  [3:0] rd4,
  input  [31:0] immI32,
  input  is_addi,
  input  is_jalr,
  output gpr_wen,
  output [3:0] waddr,
  output [31:0] wdata,
  output pc_sel,
  output [31:0] pc_target
);

  wire comparator_1_eq, not_1_out, or_1_out;
  wire [0:0] adder_1_out;

  Adder #(.width(32)) adder_1 (.a(rdata1), .b(immI32), .out({pc_target[31:1], adder_1_out[0]}));  // open: cin, cout
  Comparator #(.width(4)) comparator_1 (.a(rd4), .b(4'b0000), .eq(comparator_1_eq));  // open: gt, lt
  or or_1 (or_1_out, is_addi, is_jalr);
  not not_1 (not_1_out, comparator_1_eq);
  and and_1 (gpr_wen, or_1_out, not_1_out);
  Multiplexer #(.width(32)) multiplexer_1 (
    .in0({pc_target[31:1], adder_1_out[0]}), .in1(pc_plus4), .out(wdata), .sel(is_jalr));

  assign pc_sel = is_jalr;
  assign pc_target[0] = 1'b0;
  assign waddr = rd4;
endmodule

module DecodeCore (
  input  [31:0] inst,
  output [6:0] opcode,
  output [3:0] rd4,
  output [2:0] funct3,
  output [3:0] rs1_4,
  output [31:0] immI32,
  output is_addi,
  output is_jalr,
  output [3:0] rs2_4,
  output [6:0] func7,
  output [31:0] immU32,
  output is_add,
  output is_lui,
  output [31:0] immS32,
  output is_lw,
  output is_sw,
  output is_lbu,
  output is_sb
);

  wire comparator_1_eq, comparator_2_eq, comparator_3_eq, comparator_4_eq, comparator_5_eq, comparator_6_eq,
       comparator_7_eq, comparator_9_eq, comparator_10_eq, comparator_11_eq, comparator_12_eq,
       comparator_13_eq, comparator_14_eq, comparator_15_eq, comparator_16_eq;

  assign immI32 = {{20{inst[31]}}, inst[31:20]};  // Bit_Extender bit_extender_1
  Comparator #(.width(7)) comparator_1 (.a(inst[6:0]), .b(7'b0010011), .eq(comparator_1_eq));  // open: gt, lt
  Comparator #(.width(3)) comparator_2 (.a(inst[14:12]), .b(3'b000), .eq(comparator_2_eq));  // open: gt, lt
  Comparator #(.width(7)) comparator_3 (.a(inst[6:0]), .b(7'b1100111), .eq(comparator_3_eq));  // open: gt, lt
  Comparator #(.width(3)) comparator_4 (.a(inst[14:12]), .b(3'b000), .eq(comparator_4_eq));  // open: gt, lt
  Comparator #(.width(7)) comparator_5 (.a(inst[6:0]), .b(7'b0110011), .eq(comparator_5_eq));  // open: gt, lt
  Comparator #(.width(3)) comparator_6 (.a(inst[14:12]), .b(3'b000), .eq(comparator_6_eq));  // open: gt, lt
  Comparator #(.width(7)) comparator_7 (.a(inst[31:25]), .b({7{1'b0}}), .eq(comparator_7_eq));  // open: gt, lt
  Comparator #(.width(7)) comparator_8 (.a(inst[6:0]), .b(7'b0110111), .eq(is_lui));  // open: gt, lt
  assign immS32 = {{20{inst[31]}}, {inst[31:25], inst[11:7]}};  // Bit_Extender bit_extender_2
  Comparator #(.width(7)) comparator_9 (.a(inst[6:0]), .b(7'b0000011), .eq(comparator_9_eq));  // open: gt, lt
  Comparator #(.width(3)) comparator_10 (.a(inst[14:12]), .b(3'b010), .eq(comparator_10_eq));  // open: gt, lt
  Comparator #(.width(7)) comparator_11 (.a(inst[6:0]), .b(7'b0100011), .eq(comparator_11_eq));  // open: gt, lt
  Comparator #(.width(3)) comparator_12 (.a(inst[14:12]), .b(3'b010), .eq(comparator_12_eq));  // open: gt, lt
  Comparator #(.width(7)) comparator_13 (.a(inst[6:0]), .b(7'b0000011), .eq(comparator_13_eq));  // open: gt, lt
  Comparator #(.width(3)) comparator_14 (.a(inst[14:12]), .b(3'b100), .eq(comparator_14_eq));  // open: gt, lt
  Comparator #(.width(7)) comparator_15 (.a(inst[6:0]), .b(7'b0100011), .eq(comparator_15_eq));  // open: gt, lt
  Comparator #(.width(3)) comparator_16 (.a(inst[14:12]), .b(3'b000), .eq(comparator_16_eq));  // open: gt, lt
  and and_1 (is_addi, comparator_1_eq, comparator_2_eq);
  and and_2 (is_jalr, comparator_3_eq, comparator_4_eq);
  and and_3 (is_add, comparator_5_eq, comparator_6_eq, comparator_7_eq);
  and and_4 (is_lw, comparator_9_eq, comparator_10_eq);
  and and_5 (is_sw, comparator_11_eq, comparator_12_eq);
  and and_6 (is_lbu, comparator_13_eq, comparator_14_eq);
  and and_7 (is_sb, comparator_15_eq, comparator_16_eq);

  assign func7 = inst[31:25];
  assign funct3 = inst[14:12];
  assign immU32 = {inst[31:12], {12{1'b0}}};
  assign opcode = inst[6:0];
  assign rd4 = inst[10:7];
  assign rs1_4 = inst[18:15];
  assign rs2_4 = inst[23:20];
endmodule

module ExecCore (
  input  [31:0] pc_plus4,
  input  [31:0] rdata1,
  input  [3:0] rd4,
  input  [31:0] immI32,
  input  is_addi,
  input  is_jalr,
  input  [31:0] rdata2,
  input  is_add,
  input  is_lui,
  input  [31:0] immU32,
  output gpr_wen,
  output [3:0] waddr,
  output [31:0] wdata,
  output pc_sel,
  output [31:0] pc_target
);

  wire comparator_1_eq, not_1_out, or_1_out;
  wire [0:0] adder_2_out;
  wire [31:0] adder_1_out, multiplexer_1_out, multiplexer_2_out;

  Adder #(.width(32)) adder_1 (.a(rdata1), .b(rdata2), .out(adder_1_out));  // open: cin, cout
  Adder #(.width(32)) adder_2 (.a(rdata1), .b(immI32), .out({pc_target[31:1], adder_2_out[0]}));  // open: cin, cout
  Comparator #(.width(4)) comparator_1 (.a(rd4), .b(4'b0000), .eq(comparator_1_eq));  // open: gt, lt
  or or_1 (or_1_out, is_add, is_addi, is_lui, is_jalr);
  not not_1 (not_1_out, comparator_1_eq);
  and and_1 (gpr_wen, or_1_out, not_1_out);
  Multiplexer #(.width(32)) multiplexer_1 (
    .in0({pc_target[31:1], adder_2_out[0]}), .in1(adder_1_out), .out(multiplexer_1_out), .sel(is_add));
  Multiplexer #(.width(32)) multiplexer_2 (
    .in0(multiplexer_1_out), .in1(immU32), .out(multiplexer_2_out), .sel(is_lui));
  Multiplexer #(.width(32)) multiplexer_3 (.in0(multiplexer_2_out), .in1(pc_plus4), .out(wdata), .sel(is_jalr));

  assign pc_sel = is_jalr;
  assign pc_target[0] = 1'b0;
  assign waddr = rd4;

  // Notes on the sheet:
  //   add_res
  //   addi_res
endmodule

module MemAccessIF (
  input  [3:0] rd4,
  input  [31:0] rdata1,
  input  [31:0] rdata2,
  input  [31:0] immI32,
  input  [31:0] immS32,
  input  is_lw,
  input  is_sw,
  input  [31:0] ram_rdata,
  input  is_lbu,
  input  is_sb,
  output mem_gpr_wen,
  output [3:0] mem_waddr,
  output [31:0] mem_wdata,
  output [17:0] ram_addr,
  output ram_wen,
  output [3:0] ram_be,
  output [31:0] ram_wdata,
  output [31:0] eff_addr
);

  wire and_2_out, and_3_out, and_4_out, and_5_out, comparator_1_eq, comparator_2_eq, comparator_3_eq,
       comparator_4_eq, comparator_5_eq, not_1_out, or_1_out, or_7_out;
  wire [7:0] multiplexer_4_out;
  wire [31:0] adder_1_out, adder_2_out, bit_extender_1_out;

  Adder #(.width(32)) adder_1 (.a(rdata1), .b(immI32), .out(adder_1_out));  // open: cin, cout
  Adder #(.width(32)) adder_2 (.a(rdata1), .b(immS32), .out(adder_2_out));  // open: cin, cout
  or or_1 (or_1_out, is_sw, is_sb);
  Multiplexer #(.width(32)) multiplexer_1 (.in0(adder_1_out), .in1(adder_2_out), .out(eff_addr), .sel(or_1_out));
  or or_2 (ram_be[0], is_sw, and_2_out);
  or or_3 (ram_be[1], is_sw, and_3_out);
  or or_4 (ram_be[2], is_sw, and_4_out);
  or or_5 (ram_be[3], is_sw, and_5_out);
  Comparator #(.width(4)) comparator_1 (.a(rd4), .b(4'b0000), .eq(comparator_1_eq));  // open: gt, lt
  not not_1 (not_1_out, comparator_1_eq);
  Comparator #(.width(2)) comparator_2 (.a(eff_addr[1:0]), .b(2'b00), .eq(comparator_2_eq));  // open: gt, lt
  Comparator #(.width(2)) comparator_3 (.a(eff_addr[1:0]), .b(2'b01), .eq(comparator_3_eq));  // open: gt, lt
  Comparator #(.width(2)) comparator_4 (.a(eff_addr[1:0]), .b(2'b10), .eq(comparator_4_eq));  // open: gt, lt
  Comparator #(.width(2)) comparator_5 (.a(eff_addr[1:0]), .b(2'b11), .eq(comparator_5_eq));  // open: gt, lt
  or or_6 (ram_wen, is_sw, is_sb);
  Multiplexer #(.width(32)) multiplexer_2 (
    .in0({rdata2[7:0], rdata2[7:0], rdata2[7:0], rdata2[7:0]}), .in1(rdata2), .out(ram_wdata), .sel(is_sw));
  or or_7 (or_7_out, is_lw, is_lbu);
  and and_1 (mem_gpr_wen, not_1_out, or_7_out);
  Multiplexer #(.width(32)) multiplexer_3 (.in0(ram_rdata), .in1(bit_extender_1_out), .out(mem_wdata), .sel(is_lbu));
  Multiplexer #(.select(2), .width(8)) multiplexer_4 (
    .in0(ram_rdata[7:0]), .in1(ram_rdata[15:8]), .in2(ram_rdata[23:16]), .in3(ram_rdata[31:24]),
    .out(multiplexer_4_out), .sel(eff_addr[1:0]));
  and and_2 (and_2_out, is_sb, comparator_2_eq);
  and and_3 (and_3_out, is_sb, comparator_3_eq);
  and and_4 (and_4_out, is_sb, comparator_4_eq);
  and and_5 (and_5_out, is_sb, comparator_5_eq);
  assign bit_extender_1_out = {{24{1'b0}}, multiplexer_4_out};  // Bit_Extender bit_extender_1

  assign mem_waddr = rd4;
  assign ram_addr = eff_addr[19:2];

  // Notes on the sheet:
  //   addr_load
  //   addr_store
  //   byte_sel
endmodule

module CycleCounter64 (
  input  clk,
  input  reset,
  input  en,
  output [63:0] count
);

  wire [63:0] adder_1_out;

  Register #(.width(64)) register_1 (.D(adder_1_out), .en(en), .clk(clk), .Q(count), .clr(reset));
  Adder #(.width(64)) adder_1 (.a(64'h1), .b(count), .out(adder_1_out));  // open: cin, cout
endmodule
